// Logisim project 1 Transistor Gates.circ as structural Verilog: 11 circuits, main circuit CMOS_and
module NMOS_not (
  input  X,
  output Z
);

  Pull_Resistor #(.pull(1)) pull_resistor_1 (.node(Z));
  Transistor transistor_1 (.in(1'b0), .out(Z), .gate(X));
endmodule

module NPN (
  input  A,
  input  B,
  output Z
);

  wire pull_resistor_1_node, transistor_2_out;

  Transistor #(.\type ("n")) transistor_1 (.in(transistor_2_out), .out(Z), .gate(A));
  Transistor #(.\type ("n")) transistor_2 (.in(pull_resistor_1_node), .out(transistor_2_out), .gate(B));
  Pull_Resistor pull_resistor_1 (.node(pull_resistor_1_node));
endmodule

module PNP (
  input  A,
  input  B,
  output Z
);

  wire pull_resistor_1_node;

  Pull_Resistor #(.pull(1)) pull_resistor_1 (.node(pull_resistor_1_node));
  Transistor transistor_1 (.in(pull_resistor_1_node), .out(Z), .gate(B));
  Transistor transistor_2 (.in(pull_resistor_1_node), .out(Z), .gate(A));
endmodule

module CMOS_and (
  input  X,
  input  Y,
  output Z
);

  wire transistor_1_out, transistor_4_out;

  Transistor transistor_1 (.in(1'b1), .out(transistor_1_out), .gate(Y));
  Transistor transistor_2 (.in(1'b1), .out(transistor_1_out), .gate(X));
  Transistor #(.\type ("n")) transistor_3 (.in(transistor_4_out), .out(transistor_1_out), .gate(X));
  Transistor #(.\type ("n")) transistor_4 (.in(1'b0), .out(transistor_4_out), .gate(Y));
  Transistor transistor_5 (.in(1'b1), .out(Z), .gate(transistor_1_out));
  Transistor #(.\type ("n")) transistor_6 (.in(1'b0), .out(Z), .gate(transistor_1_out));

  // Notes on the sheet:
  //   Vdd
  //   Vss
endmodule

module CMOS_nand (
  input  X,
  input  Y,
  output Z
);

  wire transistor_4_out;

  Transistor transistor_1 (.in(1'b1), .out(Z), .gate(Y));
  Transistor transistor_2 (.in(1'b1), .out(Z), .gate(X));
  Transistor #(.\type ("n")) transistor_3 (.in(transistor_4_out), .out(Z), .gate(X));
  Transistor #(.\type ("n")) transistor_4 (.in(1'b0), .out(transistor_4_out), .gate(Y));

  // Notes on the sheet:
  //   Vdd
  //   Vss
endmodule

module CMOS_nor (
  input  X,
  input  Y,
  output Z
);

  wire transistor_1_out;

  Transistor transistor_1 (.in(1'b1), .out(transistor_1_out), .gate(X));
  Transistor transistor_2 (.in(transistor_1_out), .out(Z), .gate(Y));
  Transistor #(.\type ("n")) transistor_3 (.in(1'b0), .out(Z), .gate(Y));
  Transistor #(.\type ("n")) transistor_4 (.in(1'b0), .out(Z), .gate(X));

  // Notes on the sheet:
  //   Vdd
  //   Vss
endmodule

module CMOS_or (
  input  X,
  input  Y,
  output Z
);

  wire transistor_1_out, transistor_2_out;

  Transistor transistor_1 (.in(1'b1), .out(transistor_1_out), .gate(X));
  Transistor transistor_2 (.in(transistor_1_out), .out(transistor_2_out), .gate(Y));
  Transistor #(.\type ("n")) transistor_3 (.in(1'b0), .out(transistor_2_out), .gate(Y));
  Transistor #(.\type ("n")) transistor_4 (.in(1'b0), .out(transistor_2_out), .gate(X));
  Transistor transistor_5 (.in(1'b1), .out(Z), .gate(transistor_2_out));
  Transistor #(.\type ("n")) transistor_6 (.in(1'b0), .out(Z), .gate(transistor_2_out));

  // Notes on the sheet:
  //   Vdd
  //   Vss
endmodule

module CMOS_not (
  input  X,
  output Z
);

  Transistor transistor_1 (.in(1'b1), .out(Z), .gate(X));
  Transistor #(.\type ("n")) transistor_2 (.in(1'b0), .out(Z), .gate(X));

  // Notes on the sheet:
  //   Vdd
  //   Vss
endmodule

module CMOS_not_compact (
  input  X,
  output Z
);

  Transistor transistor_1 (.in(1'b1), .out(Z), .gate(X));
  Transistor #(.\type ("n")) transistor_2 (.in(1'b0), .out(Z), .gate(X));

  // Notes on the sheet:
  //   Vdd
  //   Vss
endmodule

module T_xor (
  input  X,
  input  Y,
  output Z
);

  wire cmos_and_1_z, cmos_and_2_z, cmos_not_1_z;

  CMOS_not cmos_not_1 (.X(Y), .Z(cmos_not_1_z));
  CMOS_not cmos_not_2 (.X(X), .Z(cmos_not_1_z));
  CMOS_and cmos_and_1 (.Y(cmos_not_1_z), .X(Y), .Z(cmos_and_1_z));
  CMOS_and cmos_and_2 (.Y(X), .X(cmos_not_1_z), .Z(cmos_and_2_z));
  CMOS_or cmos_or_1 (.Y(cmos_and_2_z), .X(cmos_and_1_z), .Z(Z));
endmodule

module MOS_test (
  input  X,
  input  Y,
  output out_3,
  output out_4,
  output out_5,
  output out_6,
  output out_7,
  output out_8
);

  CMOS_not cmos_not_1 (.X(X), .Z(out_3));
  CMOS_and cmos_and_1 (.Y(X), .X(X), .Z(out_4));
  CMOS_or cmos_or_1 (.Y(X), .X(X), .Z(out_5));
  CMOS_nand cmos_nand_1 (.Y(X), .X(X), .Z(out_6));
  CMOS_nor cmos_nor_1 (.Y(X), .X(X), .Z(out_7));
  T_xor t_xor_1 (.Y(X), .X(X), .Z(out_8));

  assign Y = X;
endmodule
