// Logisim project 2 Arithmetic.circ as structural Verilog: 8 circuits, main circuit HalfAdder
module HalfAdder (
  input  X,
  input  Y,
  output S,
  output C
);

  xor xor_1 (S, X, Y);
  and and_1 (C, X, Y);
endmodule

module Adder_1b (
  input  Ci,
  input  X,
  input  Y,
  output S,
  output Co
);

  wire halfadder_1_c, halfadder_2_c, halfadder_2_s;

  HalfAdder halfadder_1 (.X(Ci), .Y(halfadder_2_s), .C(halfadder_1_c), .S(S));
  HalfAdder halfadder_2 (.X(X), .Y(Y), .C(halfadder_2_c), .S(halfadder_2_s));
  or or_1 (Co, halfadder_1_c, halfadder_2_c);
endmodule

module Adder_1byte (
  input  Ci,
  input  [3:0] X,
  input  [3:0] Y,
  output [3:0] S,
  output Co
);

  wire adder_1b_1_co, adder_1b_2_co, adder_1b_3_co;

  Adder_1b adder_1b_1 (.Ci(Ci), .X(X[0]), .Y(Y[0]), .S(S[0]), .Co(adder_1b_1_co));
  Adder_1b adder_1b_2 (.Ci(adder_1b_1_co), .X(X[1]), .Y(Y[1]), .S(S[1]), .Co(adder_1b_2_co));
  Adder_1b adder_1b_3 (.Ci(adder_1b_2_co), .X(X[2]), .Y(Y[2]), .S(S[2]), .Co(adder_1b_3_co));
  Adder_1b adder_1b_4 (.Ci(adder_1b_3_co), .X(X[3]), .Y(Y[3]), .S(S[3]), .Co(Co));
endmodule

module HalfSubtractor (
  input  X,
  input  Y,
  output B,
  output D
);

  wire not_1_out;

  not not_1 (not_1_out, X);
  xor xor_1 (D, X, Y);
  and and_1 (B, not_1_out, Y);
endmodule

module Subtractor_1b (
  input  X,
  input  Y,
  input  Bin,
  output Bout,
  output D
);

  wire halfsubtractor_1_b, halfsubtractor_1_d, halfsubtractor_2_b;

  HalfSubtractor halfsubtractor_1 (.X(X), .Y(Y), .D(halfsubtractor_1_d), .B(halfsubtractor_1_b));
  HalfSubtractor halfsubtractor_2 (.X(halfsubtractor_1_d), .Y(Bin), .D(D), .B(halfsubtractor_2_b));
  or or_1 (Bout, halfsubtractor_1_b, halfsubtractor_2_b);
endmodule

module Subtractor_1byte (
  input  Bi,
  input  [3:0] X,
  input  [3:0] Y,
  output [3:0] D,
  output Bo
);

  wire subtractor_1b_1_bout, subtractor_1b_2_bout, subtractor_1b_3_bout;

  Subtractor_1b subtractor_1b_1 (.X(X[0]), .Y(Y[0]), .Bin(Bi), .Bout(subtractor_1b_1_bout), .D(D[0]));
  Subtractor_1b subtractor_1b_2 (.X(X[1]), .Y(Y[1]), .Bin(subtractor_1b_1_bout), .Bout(subtractor_1b_2_bout), .D(D[1]));
  Subtractor_1b subtractor_1b_3 (.X(X[2]), .Y(Y[2]), .Bin(subtractor_1b_2_bout), .Bout(subtractor_1b_3_bout), .D(D[2]));
  Subtractor_1b subtractor_1b_4 (.X(X[3]), .Y(Y[3]), .Bin(subtractor_1b_3_bout), .Bout(Bo), .D(D[3]));
endmodule

module Comparator_1b (
  input  A,
  input  B,
  output Ls,
  output Eq,
  output Gt
);

  wire not_1_out, not_2_out;

  not not_1 (not_1_out, A);
  not not_2 (not_2_out, B);
  and and_1 (Ls, not_1_out, B);
  xnor xnor_1 (Eq, A, B);
  and and_2 (Gt, A, not_2_out);
endmodule

module Comparator_1byte (
  input  [3:0] A,
  input  [3:0] B,
  output Eq,
  output Gt,
  output Lt
);

  wire and_2_out, and_3_out, and_4_out, and_5_out, and_6_out, and_7_out, comparator_1b_1_eq,
       comparator_1b_1_gt, comparator_1b_1_ls, comparator_1b_2_eq, comparator_1b_2_gt, comparator_1b_2_ls,
       comparator_1b_3_eq, comparator_1b_3_gt, comparator_1b_3_ls, comparator_1b_4_eq, comparator_1b_4_gt,
       comparator_1b_4_ls;

  Comparator_1b comparator_1b_1 (
    .A(A[0]), .B(B[0]), .Eq(comparator_1b_1_eq), .Gt(comparator_1b_1_gt), .Ls(comparator_1b_1_ls));
  Comparator_1b comparator_1b_2 (
    .A(A[1]), .B(B[1]), .Eq(comparator_1b_2_eq), .Gt(comparator_1b_2_gt), .Ls(comparator_1b_2_ls));
  Comparator_1b comparator_1b_3 (
    .A(A[2]), .B(B[2]), .Eq(comparator_1b_3_eq), .Gt(comparator_1b_3_gt), .Ls(comparator_1b_3_ls));
  Comparator_1b comparator_1b_4 (
    .A(A[3]), .B(B[3]), .Eq(comparator_1b_4_eq), .Gt(comparator_1b_4_gt), .Ls(comparator_1b_4_ls));
  and and_1 (Eq, comparator_1b_1_eq, comparator_1b_2_eq, comparator_1b_3_eq, comparator_1b_4_eq);
  or or_1 (Gt, comparator_1b_4_gt, and_2_out, and_3_out, and_4_out);
  and and_2 (and_2_out, comparator_1b_4_eq, comparator_1b_3_gt);
  and and_3 (and_3_out, comparator_1b_4_eq, comparator_1b_3_eq, comparator_1b_2_gt);
  and and_4 (and_4_out, comparator_1b_4_eq, comparator_1b_3_eq, comparator_1b_2_eq, comparator_1b_1_gt);
  or or_2 (Lt, comparator_1b_4_ls, and_5_out, and_6_out, and_7_out);
  and and_5 (and_5_out, comparator_1b_4_eq, comparator_1b_3_ls);
  and and_6 (and_6_out, comparator_1b_4_eq, comparator_1b_3_eq, comparator_1b_2_ls);
  and and_7 (and_7_out, comparator_1b_4_eq, comparator_1b_3_eq, comparator_1b_2_eq, comparator_1b_1_ls);
endmodule
