// Logisim project 2 BCD_LED.circ as structural Verilog: 3 circuits, main circuit BCD_HEX_LED
module HEX_LED (
  input  a,
  input  b,
  input  c,
  input  d,
  input  e,
  input  f,
  input  g,
  input  dp
);

  _7_Segment_Display O (.g(g), .f(f), .a(a), .b(b), .e(e), .d(d), .c(c), .dp(dp));
endmodule

module BCD_HEX_LED (
  input  idp,
  input  iA,
  input  iB,
  input  iC,
  input  iD
);

  wire A_B_out, A_C_out, A_D_out, A_nB_nC_out, A_nB_out, A_nC_D_out, A_nC_out, A_nD_out, B_C_nD_out, B_C_out,
       B_nC_D_out, B_nD_out, C_nD_out, nA_B_D_out, nA_B_nC_out, nA_B_out, nA_C_D_out, nA_C_out, nA_D_out,
       nA_nB_nD_out, nA_nC_nD_out, nA_nC_out, nB_C_D_out, nB_C_out, nB_nC_out, nB_nD_out, nC_D_out,
       nC_nD_out, not_1_out, not_2_out, not_3_out, not_4_out, or_1_out, or_2_out, or_3_out, or_4_out,
       or_5_out, or_6_out, or_7_out;

  not not_1 (not_1_out, iA);
  not not_2 (not_2_out, iB);
  not not_3 (not_3_out, iC);
  not not_4 (not_4_out, iD);
  and A_nB_nC (A_nB_nC_out, iA, not_2_out, not_3_out);
  and nA_B_D (nA_B_D_out, not_1_out, iB, iD);
  and A_nD (A_nD_out, iA, not_4_out);
  and nA_C (nA_C_out, not_1_out, iC);
  and B_C (B_C_out, iB, iC);
  and nB_nD (nB_nD_out, not_2_out, not_4_out);
  and nA_nC_nD (nA_nC_nD_out, not_1_out, not_3_out, not_4_out);
  and nA_C_D (nA_C_D_out, not_1_out, iC, iD);
  and A_nC_D (A_nC_D_out, iA, not_3_out, iD);
  and nB_nC (nB_nC_out, not_2_out, not_3_out);
  and nA_nC (nA_nC_out, not_1_out, not_3_out);
  and nA_D (nA_D_out, not_1_out, iD);
  and nC_D (nC_D_out, not_3_out, iD);
  and nA_B (nA_B_out, not_1_out, iB);
  and A_nB (A_nB_out, iA, not_2_out);
  and nA_nB_nD (nA_nB_nD_out, not_1_out, not_2_out, not_4_out);
  and nB_C_D (nB_C_D_out, not_2_out, iC, iD);
  and B_nC_D (B_nC_D_out, iB, not_3_out, iD);
  and B_C_nD (B_C_nD_out, iB, iC, not_4_out);
  and A_nC (A_nC_out, iA, not_3_out);
  and C_nD (C_nD_out, iC, not_4_out);
  and A_C (A_C_out, iA, iC);
  and A_B (A_B_out, iA, iB);
  and nA_B_nC (nA_B_nC_out, not_1_out, iB, not_3_out);
  and nC_nD (nC_nD_out, not_3_out, not_4_out);
  and B_nD (B_nD_out, iB, not_4_out);
  and nB_C (nB_C_out, not_2_out, iC);
  and A_D (A_D_out, iA, iD);
  or or_1 (or_1_out, A_nB_nC_out, nA_B_D_out, A_nD_out, nA_C_out, B_C_out, nB_nD_out);
  or or_2 (or_2_out, nA_nC_nD_out, nA_C_D_out, A_nC_D_out, nB_nD_out, nB_nC_out);
  or or_3 (or_3_out, nA_nC_out, nA_D_out, nC_D_out, nA_B_out, A_nB_out);
  or or_4 (or_4_out, nA_nB_nD_out, nB_C_D_out, B_nC_D_out, B_C_nD_out, A_nC_out);
  HEX_LED hex_led_1 (
    .a(or_1_out), .b(or_2_out), .c(or_3_out), .d(or_4_out), .e(or_5_out), .f(or_6_out), .g(or_7_out), .dp(idp));
  or or_5 (or_5_out, nB_nD_out, C_nD_out, A_C_out, A_B_out);
  or or_6 (or_6_out, A_nB_out, A_C_out, nA_B_nC_out, nC_nD_out, B_nD_out);
  or or_7 (or_7_out, A_nB_out, C_nD_out, nA_B_nC_out, nB_C_out, A_D_out);
endmodule

module LED_byte (
  input  [3:0] D,
  input  dp
);

  BCD_HEX_LED bcd_hex_led_1 (.iD(D[0]), .idp(dp), .iA(D[3]), .iB(D[2]), .iC(D[1]));
endmodule
