// Logisim project 2 FlipFlops.circ as structural Verilog: 13 circuits, main circuit EdgeDFlipFlop
module NandSRLatch (
  input  nS,
  input  nR,
  output Q,
  output nQ
);

  nand nand_1 (Q, nS, nQ);
  nand nand_2 (nQ, Q, nR);
endmodule

module NorSRLatch (
  input  R,
  input  S,
  output Q,
  output nQ
);

  nor nor_1 (Q, R, nQ);
  nor nor_2 (nQ, Q, S);
endmodule

module JKFlipFlop (
  input  J,
  input  CLK,
  input  K,
  input  Rst,
  output Q,
  output nQ
);

  wire and_1_out, and_2_out, and_3_out, and_4_out, nor_1_out, nor_2_out, not_1_out;

  and and_1 (and_1_out, nQ, J, CLK);
  not not_1 (not_1_out, CLK);
  and and_2 (and_2_out, CLK, K, Q);
  nor nor_1 (nor_1_out, and_1_out, nor_2_out);
  nor nor_2 (nor_2_out, nor_1_out, Rst, and_2_out);
  and and_3 (and_3_out, nor_1_out, not_1_out);
  and and_4 (and_4_out, not_1_out, nor_2_out);
  nor nor_3 (Q, and_3_out, nQ);
  LED led_1 (.in(Q));
  nor nor_4 (nQ, Q, Rst, and_4_out);
endmodule

module TFlopFlop (
  input  T,
  input  CLK,
  input  Rst,
  output Q,
  output nQ
);

  LED led_1 (.in(Q));
  JKFlipFlop jkflipflop_1 (.J(T), .CLK(CLK), .K(T), .Rst(Rst), .Q(Q), .nQ(nQ));
endmodule

module GatedSRLatch (
  input  R,
  input  E,
  input  S,
  output Q,
  output nQ
);

  wire and_1_out, and_2_out;

  and and_1 (and_1_out, R, E);
  and and_2 (and_2_out, E, S);
  NorSRLatch norsrlatch_1 (.S(and_2_out), .R(and_1_out), .nQ(nQ), .Q(Q));
endmodule

module DLatch (
  input  D,
  input  E,
  output Q,
  output nQ
);

  wire not_1_out;

  LED led_1 (.in(Q));
  GatedSRLatch gatedsrlatch_1 (.R(not_1_out), .E(E), .S(D), .Q(Q), .nQ(nQ));
  not not_1 (not_1_out, D);
endmodule

module PRFlipFlop (
  input  S,
  input  D,
  input  E,
  input  R,
  output Q,
  output nQ
);

  wire nand_1_out, nand_2_out, nand_3_out, nand_4_out, nand_5_out, nand_6_out, not_1_out, not_2_out,
       not_3_out, not_4_out;

  not not_1 (not_1_out, S);
  not not_2 (not_2_out, D);
  not not_3 (not_3_out, R);
  nand nand_1 (nand_1_out, D, E);
  nand nand_2 (nand_2_out, not_1_out, nand_1_out, nand_2_out);
  nand nand_3 (nand_3_out, not_2_out, E);
  nand nand_4 (nand_4_out, nand_2_out, nand_3_out, not_3_out);
  not not_4 (not_4_out, E);
  nand nand_5 (nand_5_out, nand_2_out, not_4_out);
  nand nand_6 (nand_6_out, nand_4_out, not_4_out);
  nand nand_7 (Q, not_1_out, nand_5_out, nQ);
  nand nand_8 (nQ, Q, nand_6_out, not_3_out);
  LED led_1 (.in(Q));
endmodule

module EdgeDFlipFlop (
  input  D,
  input  CLK,
  output Q,
  output nQ
);

  wire dlatch_1_q, not_1_out;

  DLatch dlatch_1 (.D(D), .E(CLK), .Q(dlatch_1_q));  // open: nQ
  DLatch dlatch_2 (.D(dlatch_1_q), .E(not_1_out), .nQ(nQ), .Q(Q));
  not not_1 (not_1_out, CLK);
endmodule

module EdgeSRFlipFlop (
  input  S,
  input  CLK,
  input  D,
  input  qR,
  output Q,
  output nQ
);

  wire not_1_out, not_2_out, P1_out, P2_out, P3_out, P4_out;

  not not_1 (not_1_out, S);
  not not_2 (not_2_out, qR);
  nand P1 (P1_out, not_1_out, P4_out, P2_out);
  nand P2 (P2_out, P1_out, not_2_out, CLK);
  nand P3 (P3_out, P2_out, CLK, P4_out);
  nand P4 (P4_out, P3_out, D, not_2_out);
  LED led_1 (.in(Q));
  nand P5 (Q, not_1_out, P2_out, nQ);
  nand P6 (nQ, Q, P3_out, not_2_out);
endmodule

module SFlipFlop (
  input  S,
  input  D,
  input  E,
  input  R,
  output Q,
  output nQ
);

  wire and_1_out, and_2_out, nor_1_out, nor_2_out, not_1_out;

  not not_1 (not_1_out, D);
  and and_1 (and_1_out, D, E);
  and and_2 (and_2_out, not_1_out, E);
  LED led_1 (.in(Q));
  nor nor_1 (nor_1_out, S, and_1_out);
  NandSRLatch nandsrlatch_1 (.nR(nor_2_out), .nS(nor_1_out), .nQ(nQ), .Q(Q));
  nor nor_2 (nor_2_out, and_2_out, R);
endmodule

module EdgePCFlipFlop (
  input  S,
  input  D,
  input  E,
  input  R,
  output Q,
  output nQ
);

  wire and_1_out, and_2_out, nand_1_out, nand_2_out, not_1_out, not_2_out, not_3_out;

  not not_1 (not_1_out, D);
  not not_2 (not_2_out, S);
  nand nand_1 (nand_1_out, D, E);
  nand nand_2 (nand_2_out, not_1_out, E);
  not not_3 (not_3_out, R);
  and and_1 (and_1_out, not_2_out, nand_1_out);
  or or_1 (Q, ~and_1_out, ~nQ);  // OR_Gate
  and and_2 (and_2_out, nand_2_out, not_3_out);
  or or_2 (nQ, ~Q, ~and_2_out);  // OR_Gate
  LED led_1 (.in(Q));
endmodule

module DFlopFlop (
  input  S,
  input  D,
  input  CLK,
  input  R,
  output Q,
  output nQ
);

  wire nand_1_out, nand_2_out, not_1_out, not_2_out;

  not not_1 (not_1_out, S);
  not not_2 (not_2_out, R);
  nand nand_1 (nand_1_out, D, CLK, not_2_out);
  nand nand_2 (nand_2_out, nand_1_out, not_1_out, CLK);
  nand nand_3 (Q, not_1_out, nand_1_out, nQ);
  nand nand_4 (nQ, Q, nand_2_out, not_2_out);
  LED led_1 (.in(Q));
endmodule

module FlipFlops_test (
  input  D,
  input  E
);

  wire dflopflop_1_nq, dflopflop_1_q, edgepcflipflop_1_nq, edgepcflipflop_1_q, edgesrflipflop_1_nq,
       edgesrflipflop_1_q, Rst_out, Set_out, sflipflop_1_nq, sflipflop_1_q;

  Button Set (.out(Set_out));
  Button Rst (.out(Rst_out));
  SFlipFlop sflipflop_1 (.S(Set_out), .R(Rst_out), .D(D), .E(E), .Q(sflipflop_1_q), .nQ(sflipflop_1_nq));
  EdgePCFlipFlop edgepcflipflop_1 (
    .R(Rst_out), .S(Set_out), .D(D), .E(E), .Q(edgepcflipflop_1_q), .nQ(edgepcflipflop_1_nq));
  EdgeSRFlipFlop edgesrflipflop_1 (
    .CLK(E), .D(D), .qR(Rst_out), .S(Set_out), .Q(edgesrflipflop_1_q), .nQ(edgesrflipflop_1_nq));
  LED Q (.in(sflipflop_1_q));
  LED led_1 (.in(sflipflop_1_nq));
  LED led_2 (.in(edgepcflipflop_1_q));
  LED led_3 (.in(edgepcflipflop_1_nq));
  LED led_4 (.in(edgesrflipflop_1_q));
  LED led_5 (.in(edgesrflipflop_1_nq));
  LED led_6 (.in(dflopflop_1_q));
  DFlopFlop dflopflop_1 (.S(Set_out), .D(D), .CLK(E), .R(Rst_out), .Q(dflopflop_1_q), .nQ(dflopflop_1_nq));
  LED led_7 (.in(dflopflop_1_nq));
endmodule
