// Logisim project 2 Gates Expansion.circ as structural Verilog: 2 circuits, main circuit And_4b
module And_4b (
  input  [3:0] D,
  input  E,
  output [3:0] O
);

  and and_1 (O[0], D[0], E);
  and and_2 (O[1], D[1], E);
  and and_3 (O[2], D[2], E);
  and and_4 (O[3], D[3], E);
endmodule

module And_byte (
  input  [7:0] D,
  input  E,
  output [7:0] O
);

  and and_1 (O[0], D[0], E);
  and and_2 (O[1], D[1], E);
  and and_3 (O[2], D[2], E);
  and and_4 (O[3], D[3], E);
  and and_5 (O[4], D[4], E);
  and and_6 (O[5], D[5], E);
  and and_7 (O[6], D[6], E);
  and and_8 (O[7], D[7], E);
endmodule
