// Logisim project 3 Keyboard.circ as structural Verilog: 3 circuits, main circuit BCD_KBRD
module BCD_KBRD (
  input  I0,
  input  I1,
  input  I2,
  input  I3,
  input  I4,
  input  I5,
  input  I6,
  input  I7,
  input  I8,
  input  I9,
  output O0,
  output O1,
  output O2,
  output O3,
  output A
);

  or or_1 (O0, I1, I3, I5, I7, I9);
  or or_2 (O1, I2, I3, I6, I7);
  or or_3 (O2, I4, I5, I6, I7);
  or or_4 (O3, I8, I9);
  or or_5 (A, I9, I8, I7, I6, I5, I4, I3, I2, I1, I0);
  Hex_Digit_Display hex_digit_display_1 (.value({O3, O2, O1, O0}));  // open: dp
  LED led_1 (.in(A));
  // Probe on {O3, O2, O1, O0}
endmodule

module BCD_KBRD_byte (
  input  I0,
  input  I1,
  input  I2,
  input  I3,
  input  I4,
  input  I5,
  input  I6,
  input  I7,
  input  I8,
  input  I9,
  output [3:0] Q,
  output A
);

  BCD_KBRD bcd_kbrd_1 (
    .I1(I1), .I2(I2), .I3(I3), .I4(I4), .I5(I5), .I6(I6), .I7(I7), .I8(I8), .I9(I9), .I0(I0), .O0(Q[0]),
    .O1(Q[1]), .O2(Q[2]), .O3(Q[3]), .A(A));
  Hex_Digit_Display hex_digit_display_1 (.value(Q));  // open: dp
endmodule

module KBRD_test (
);

  wire b0_out, b1_out, b2_out, b3_out, b4_out, b5_out, b6_out, b7_out, b8_out, b9_out;

  Button b0 (.out(b0_out));
  Button b7 (.out(b7_out));
  Button b8 (.out(b8_out));
  Button b5 (.out(b5_out));
  Button b4 (.out(b4_out));
  Button b2 (.out(b2_out));
  Button b1 (.out(b1_out));
  Button b9 (.out(b9_out));
  Button b6 (.out(b6_out));
  Button b3 (.out(b3_out));
  BCD_KBRD_byte bcd_kbrd_byte_1 (
    .I4(b4_out), .I5(b5_out), .I6(b6_out), .I7(b7_out), .I8(b8_out), .I9(b9_out), .I0(b0_out), .I1(b1_out),
    .I2(b2_out), .I3(b3_out));  // open: A, Q
endmodule
