// Logisim project 3 Plexers.circ as structural Verilog: 13 circuits, main circuit Demux2
module Demux2 (
  input  S,
  input  X,
  output Y0,
  output Y1
);

  wire not_1_out;

  not not_1 (not_1_out, S);
  and and_1 (Y0, X, not_1_out);
  and and_2 (Y1, X, S);
endmodule

module Demux2_4b (
  input  [3:0] A,
  input  S,
  output [3:0] Y0,
  output [3:0] Y1
);

  wire not_1_out;

  not not_1 (not_1_out, S);
  And_4b and_4b_1 (.D(A), .E(not_1_out), .O(Y0));
  And_4b and_4b_2 (.D(A), .E(S), .O(Y1));
endmodule

module Demux2_byte (
  input  [7:0] A,
  input  S,
  output [7:0] Y0,
  output [7:0] Y1
);

  wire not_1_out;

  And_byte and_byte_1 (.D(A), .E(not_1_out), .O(Y0));
  not not_1 (not_1_out, S);
  And_byte and_byte_2 (.D(A), .E(S), .O(Y1));
endmodule

module Demux4 (
  input  S0,
  input  S1,
  input  D,
  output Y0,
  output Y1,
  output Y2,
  output Y3
);

  wire not_1_out, not_2_out;

  not not_1 (not_1_out, S0);
  not not_2 (not_2_out, S1);
  and and_1 (Y0, not_1_out, not_2_out, D);
  and and_2 (Y1, S0, not_2_out, D);
  and and_3 (Y2, not_1_out, S1, D);
  and and_4 (Y3, S0, S1, D);
endmodule

module Demux4composed (
  input  D,
  input  S1,
  input  S0,
  output Y0,
  output Y1,
  output Y2,
  output Y3
);

  wire demux2_2_y0, demux2_2_y1;

  Demux2 demux2_1 (.S(S0), .X(demux2_2_y0), .Y0(Y0), .Y1(Y1));
  Demux2 demux2_2 (.S(S1), .X(D), .Y0(demux2_2_y0), .Y1(demux2_2_y1));
  Demux2 demux2_3 (.S(S0), .X(demux2_2_y1), .Y0(Y2), .Y1(Y3));
endmodule

module Demux4_4b (
  input  [3:0] D,
  input  S0,
  input  S1,
  output [3:0] Y0,
  output [3:0] Y1,
  output [3:0] Y2,
  output [3:0] Y3
);

  wire and_1_out, and_2_out, and_3_out, and_4_out, not_1_out, not_2_out;

  not not_1 (not_1_out, S0);
  not not_2 (not_2_out, S1);
  and and_1 (and_1_out, not_1_out, not_2_out);
  And_4b and_4b_1 (.D(D), .E(and_1_out), .O(Y0));
  and and_2 (and_2_out, S0, not_2_out);
  And_4b and_4b_2 (.D(D), .E(and_2_out), .O(Y1));
  and and_3 (and_3_out, not_1_out, S1);
  and and_4 (and_4_out, S0, S1);
  And_4b and_4b_3 (.D(D), .E(and_3_out), .O(Y2));
  And_4b and_4b_4 (.D(D), .E(and_4_out), .O(Y3));
endmodule

module Demux8composed (
  input  D,
  input  S2,
  input  S1,
  input  S0,
  output Y0,
  output Y1,
  output Y2,
  output Y3,
  output Y4,
  output Y5,
  output Y6,
  output Y7
);

  wire demux2_1_y0, demux2_1_y1, demux2_2_y0, demux2_2_y1, demux2_3_y0, demux2_3_y1;

  Demux2 demux2_1 (.S(S2), .X(D), .Y0(demux2_1_y0), .Y1(demux2_1_y1));
  Demux2 demux2_2 (.S(S1), .X(demux2_1_y0), .Y0(demux2_2_y0), .Y1(demux2_2_y1));
  Demux2 demux2_3 (.S(S1), .X(demux2_1_y1), .Y0(demux2_3_y0), .Y1(demux2_3_y1));
  Demux2 demux2_4 (.S(S0), .X(demux2_2_y0), .Y0(Y0), .Y1(Y1));
  Demux2 demux2_5 (.S(S0), .X(demux2_2_y1), .Y0(Y2), .Y1(Y3));
  Demux2 demux2_6 (.S(S0), .X(demux2_3_y0), .Y0(Y4), .Y1(Y5));
  Demux2 demux2_7 (.S(S0), .X(demux2_3_y1), .Y0(Y6), .Y1(Y7));
endmodule

module Mux2 (
  input  S,
  input  B,
  input  A,
  output Y
);

  wire and_1_out, and_2_out, not_1_out;

  not not_1 (not_1_out, S);
  and and_1 (and_1_out, A, not_1_out);
  and and_2 (and_2_out, B, S);
  or or_1 (Y, and_1_out, and_2_out);
endmodule

module Mux2_4b (
  input  S,
  input  [3:0] B,
  input  [3:0] A,
  output [3:0] Y
);

  wire and_1_out, and_2_out, and_3_out, and_4_out, and_5_out, and_6_out, and_7_out, and_8_out, not_1_out;

  not not_1 (not_1_out, S);
  and and_1 (and_1_out, A[0], not_1_out);
  and and_2 (and_2_out, B[0], S);
  and and_3 (and_3_out, A[1], not_1_out);
  and and_4 (and_4_out, B[1], S);
  and and_5 (and_5_out, A[2], not_1_out);
  and and_6 (and_6_out, B[2], S);
  and and_7 (and_7_out, A[3], not_1_out);
  and and_8 (and_8_out, B[3], S);
  or or_1 (Y[0], and_1_out, and_2_out);
  or or_2 (Y[1], and_3_out, and_4_out);
  or or_3 (Y[2], and_5_out, and_6_out);
  or or_4 (Y[3], and_7_out, and_8_out);
endmodule

module Mux4 (
  input  S1,
  input  S0,
  input  D,
  input  C,
  input  B,
  input  A,
  output Y
);

  wire and_1_out, and_2_out, and_3_out, and_4_out, not_1_out, not_2_out;

  not not_1 (not_1_out, S1);
  not not_2 (not_2_out, S0);
  and and_1 (and_1_out, A, not_2_out, not_1_out);
  and and_2 (and_2_out, B, S0, not_1_out);
  and and_3 (and_3_out, C, not_2_out, S1);
  and and_4 (and_4_out, D, S0, S1);
  or or_1 (Y, and_1_out, and_2_out, and_3_out, and_4_out);
endmodule

module Mux4composed (
  input  A,
  input  B,
  input  C,
  input  D,
  input  S0,
  input  S1,
  output Y
);

  wire mux2_1_y, mux2_3_y;

  Mux2 mux2_1 (.A(A), .S(S0), .B(B), .Y(mux2_1_y));
  Mux2 mux2_2 (.A(mux2_1_y), .S(S1), .B(mux2_3_y), .Y(Y));
  Mux2 mux2_3 (.A(C), .S(S0), .B(D), .Y(mux2_3_y));
endmodule

module Mux4_4b (
  input  [3:0] A,
  input  [3:0] B,
  input  [3:0] C,
  input  [3:0] D,
  input  S0,
  input  S1,
  output [3:0] Y
);

  wire [3:0] mux2_4b_1_y, mux2_4b_2_y;

  Mux2_4b mux2_4b_1 (.A(A), .S(S0), .B(B), .Y(mux2_4b_1_y));
  Mux2_4b mux2_4b_2 (.A(C), .S(S0), .B(D), .Y(mux2_4b_2_y));
  Mux2_4b mux2_4b_3 (.A(mux2_4b_1_y), .S(S1), .B(mux2_4b_2_y), .Y(Y));
endmodule

module Mux8composed (
  input  A,
  input  B,
  input  C,
  input  D,
  input  E,
  input  F,
  input  G,
  input  H,
  input  S0,
  input  S1,
  input  S2,
  output Y
);

  wire mux4composed_1_y, mux4composed_2_y;

  Mux4composed mux4composed_1 (.C(C), .D(D), .S0(S0), .S1(S1), .A(A), .B(B), .Y(mux4composed_1_y));
  Mux4composed mux4composed_2 (.C(G), .D(H), .S0(S0), .S1(S1), .A(E), .B(F), .Y(mux4composed_2_y));
  Mux2 mux2_1 (.A(mux4composed_1_y), .S(S2), .B(mux4composed_2_y), .Y(Y));
endmodule
