// Logisim project 3 Shift Registers.circ as structural Verilog: 12 circuits, main circuit SIPO
module SIPO_test (
  input  R,
  input  CLK,
  input  D,
  input  S,
  output Q1,
  output Q2,
  output Q3,
  output Q4,
  output out_9,
  output out_10,
  output out_11,
  output out_12,
  output out_13,
  output out_14,
  output out_15,
  output out_16,
  output out_17,
  output out_18,
  output out_19,
  output out_20
);

  wire clock_1_out, or_1_out;

  Clock clock_1 (.out(clock_1_out));
  or or_1 (or_1_out, CLK, clock_1_out);
  EdgeSRFlipFlop edgesrflipflop_1 (.CLK(or_1_out), .D(D), .qR(R), .S(S), .Q(Q1));  // open: nQ
  SFlipFlop sflipflop_1 (.S(S), .R(R), .D(D), .E(or_1_out), .Q(out_9));  // open: nQ
  EdgePCFlipFlop edgepcflipflop_1 (.R(R), .S(S), .D(D), .E(or_1_out), .Q(out_13));  // open: nQ
  DFlopFlop dflopflop_1 (.S(S), .D(D), .CLK(or_1_out), .R(R), .Q(out_17));  // open: nQ
  EdgeSRFlipFlop edgesrflipflop_2 (.CLK(or_1_out), .D(Q1), .qR(R), .S(S), .Q(Q2));  // open: nQ
  EdgeSRFlipFlop edgesrflipflop_3 (.CLK(or_1_out), .D(Q2), .qR(R), .S(S), .Q(Q3));  // open: nQ
  SFlipFlop sflipflop_2 (.S(S), .R(R), .D(out_9), .E(or_1_out), .Q(out_10));  // open: nQ
  SFlipFlop sflipflop_3 (.S(S), .R(R), .D(out_10), .E(or_1_out), .Q(out_11));  // open: nQ
  EdgePCFlipFlop edgepcflipflop_2 (.R(R), .S(S), .D(out_13), .E(or_1_out), .Q(out_14));  // open: nQ
  EdgePCFlipFlop edgepcflipflop_3 (.R(R), .S(S), .D(out_14), .E(or_1_out), .Q(out_15));  // open: nQ
  DFlopFlop dflopflop_2 (.S(S), .D(out_17), .CLK(or_1_out), .R(R), .Q(out_18));  // open: nQ
  DFlopFlop dflopflop_3 (.S(S), .D(out_18), .CLK(or_1_out), .R(R), .Q(out_19));  // open: nQ
  EdgeSRFlipFlop edgesrflipflop_4 (.CLK(or_1_out), .D(Q3), .qR(R), .S(S), .Q(Q4));  // open: nQ
  SFlipFlop sflipflop_4 (.S(S), .R(R), .D(out_11), .E(or_1_out), .Q(out_12));  // open: nQ
  EdgePCFlipFlop edgepcflipflop_4 (.R(R), .S(S), .D(out_15), .E(or_1_out), .Q(out_16));  // open: nQ
  DFlopFlop dflopflop_4 (.S(S), .D(out_19), .CLK(or_1_out), .R(R), .Q(out_20));  // open: nQ
endmodule

module SISO (
  input  S,
  input  D,
  input  CLK,
  input  R,
  output Q,
  output nQ
);

  wire edgesrflipflop_1_q, edgesrflipflop_2_q, edgesrflipflop_3_q;

  EdgeSRFlipFlop edgesrflipflop_1 (.CLK(CLK), .D(D), .qR(R), .S(S), .Q(edgesrflipflop_1_q));  // open: nQ
  EdgeSRFlipFlop edgesrflipflop_2 (
    .CLK(CLK), .D(edgesrflipflop_1_q), .qR(R), .S(S), .Q(edgesrflipflop_2_q));  // open: nQ
  EdgeSRFlipFlop edgesrflipflop_3 (
    .CLK(CLK), .D(edgesrflipflop_2_q), .qR(R), .S(S), .Q(edgesrflipflop_3_q));  // open: nQ
  EdgeSRFlipFlop edgesrflipflop_4 (.CLK(CLK), .D(edgesrflipflop_3_q), .qR(R), .S(S), .Q(Q), .nQ(nQ));
endmodule

module SIPO (
  input  S,
  input  D,
  input  CLK,
  input  R,
  output Q1,
  output Q2,
  output Q3,
  output Q4
);

  EdgeSRFlipFlop edgesrflipflop_1 (.CLK(CLK), .D(D), .qR(R), .S(S), .Q(Q1));  // open: nQ
  EdgeSRFlipFlop edgesrflipflop_2 (.CLK(CLK), .D(Q1), .qR(R), .S(S), .Q(Q2));  // open: nQ
  EdgeSRFlipFlop edgesrflipflop_3 (.CLK(CLK), .D(Q2), .qR(R), .S(S), .Q(Q3));  // open: nQ
  EdgeSRFlipFlop edgesrflipflop_4 (.CLK(CLK), .D(Q3), .qR(R), .S(S), .Q(Q4));  // open: nQ
endmodule

module PISO (
  input  D1,
  input  D2,
  input  D3,
  input  D4,
  input  S,
  input  D0,
  input  CLK,
  input  WS,
  input  R,
  output Q,
  output nQ
);

  wire edgesrflipflop_1_q, edgesrflipflop_2_q, edgesrflipflop_3_q, mux2_1_y, mux2_2_y, mux2_3_y, mux2_4_y;

  Mux2 mux2_1 (.A(D1), .S(WS), .B(D0), .Y(mux2_1_y));
  EdgeSRFlipFlop edgesrflipflop_1 (.CLK(CLK), .D(mux2_1_y), .qR(R), .S(S), .Q(edgesrflipflop_1_q));  // open: nQ
  Mux2 mux2_2 (.A(D2), .S(WS), .B(edgesrflipflop_1_q), .Y(mux2_2_y));
  EdgeSRFlipFlop edgesrflipflop_2 (.CLK(CLK), .D(mux2_2_y), .qR(R), .S(S), .Q(edgesrflipflop_2_q));  // open: nQ
  Mux2 mux2_3 (.A(D3), .S(WS), .B(edgesrflipflop_2_q), .Y(mux2_3_y));
  EdgeSRFlipFlop edgesrflipflop_3 (.CLK(CLK), .D(mux2_3_y), .qR(R), .S(S), .Q(edgesrflipflop_3_q));  // open: nQ
  Mux2 mux2_4 (.A(D4), .S(WS), .B(edgesrflipflop_3_q), .Y(mux2_4_y));
  EdgeSRFlipFlop edgesrflipflop_4 (.CLK(CLK), .D(mux2_4_y), .qR(R), .S(S), .Q(Q), .nQ(nQ));
endmodule

module PIPO (
  input  D1,
  input  D2,
  input  D3,
  input  D4,
  input  S,
  input  D0,
  input  CLK,
  input  WS,
  input  R,
  output Q1,
  output Q2,
  output Q3,
  output Q4
);

  wire mux2_1_y, mux2_2_y, mux2_3_y, mux2_4_y;

  Mux2 mux2_1 (.A(D1), .S(WS), .B(D0), .Y(mux2_1_y));
  EdgeSRFlipFlop edgesrflipflop_1 (.CLK(CLK), .D(mux2_1_y), .qR(R), .S(S), .Q(Q1));  // open: nQ
  Mux2 mux2_2 (.A(D2), .S(WS), .B(Q1), .Y(mux2_2_y));
  EdgeSRFlipFlop edgesrflipflop_2 (.CLK(CLK), .D(mux2_2_y), .qR(R), .S(S), .Q(Q2));  // open: nQ
  Mux2 mux2_3 (.A(D3), .S(WS), .B(Q2), .Y(mux2_3_y));
  EdgeSRFlipFlop edgesrflipflop_3 (.CLK(CLK), .D(mux2_3_y), .qR(R), .S(S), .Q(Q3));  // open: nQ
  Mux2 mux2_4 (.A(D4), .S(WS), .B(Q3), .Y(mux2_4_y));
  EdgeSRFlipFlop edgesrflipflop_4 (.CLK(CLK), .D(mux2_4_y), .qR(R), .S(S), .Q(Q4));  // open: nQ
endmodule

module USR (
  input  D0,
  input  D1,
  input  D2,
  input  D3,
  input  M0,
  input  M1,
  input  SRI,
  input  SLI,
  input  S,
  input  CLK,
  input  R,
  output Q0,
  output Q1,
  output Q2,
  output Q3
);

  wire mux4composed_1_y, mux4composed_2_y, mux4composed_3_y, mux4composed_4_y;

  Mux4composed mux4composed_1 (.C(SLI), .D(D0), .S0(M0), .S1(M1), .A(Q0), .B(Q1), .Y(mux4composed_1_y));
  EdgeSRFlipFlop edgesrflipflop_1 (.CLK(CLK), .D(mux4composed_1_y), .qR(R), .S(S), .Q(Q0));  // open: nQ
  Mux4composed mux4composed_2 (.C(Q0), .D(D1), .S0(M0), .S1(M1), .A(Q1), .B(Q2), .Y(mux4composed_2_y));
  EdgeSRFlipFlop edgesrflipflop_2 (.CLK(CLK), .D(mux4composed_2_y), .qR(R), .S(S), .Q(Q1));  // open: nQ
  Mux4composed mux4composed_3 (.C(Q1), .D(D2), .S0(M0), .S1(M1), .A(Q2), .B(Q3), .Y(mux4composed_3_y));
  EdgeSRFlipFlop edgesrflipflop_3 (.CLK(CLK), .D(mux4composed_3_y), .qR(R), .S(S), .Q(Q2));  // open: nQ
  Mux4composed mux4composed_4 (.C(Q2), .D(D3), .S0(M0), .S1(M1), .A(Q3), .B(SRI), .Y(mux4composed_4_y));
  EdgeSRFlipFlop edgesrflipflop_4 (.CLK(CLK), .D(mux4composed_4_y), .qR(R), .S(S), .Q(Q3));  // open: nQ
endmodule

module Counter_4b (
  input  CLK,
  input  Rst,
  output [3:0] out_3
);

  wire and_1_out, and_2_out;

  JKFlipFlop jkflipflop_1 (.J(1'b1), .CLK(CLK), .K(1'b1), .Rst(Rst), .Q(out_3[0]));  // open: nQ
  and and_1 (and_1_out, out_3[0], out_3[1]);
  JKFlipFlop jkflipflop_2 (.J(out_3[0]), .CLK(CLK), .K(out_3[0]), .Rst(Rst), .Q(out_3[1]));  // open: nQ
  JKFlipFlop jkflipflop_3 (.J(and_1_out), .CLK(CLK), .K(and_1_out), .Rst(Rst), .Q(out_3[2]));  // open: nQ
  and and_2 (and_2_out, and_1_out, out_3[2]);
  JKFlipFlop jkflipflop_4 (.J(and_2_out), .CLK(CLK), .K(and_2_out), .Rst(Rst), .Q(out_3[3]));  // open: nQ
endmodule

module Ring2 (
  input  CLK,
  input  R,
  output Q1,
  output Q2
);

  EdgeSRFlipFlop edgesrflipflop_1 (.CLK(CLK), .D(Q2), .S(R), .Q(Q1));  // open: qR, nQ
  EdgeSRFlipFlop edgesrflipflop_2 (.CLK(CLK), .D(Q1), .qR(R), .Q(Q2));  // open: S, nQ
endmodule

module Ring4 (
  input  CLK,
  input  R,
  output Q1,
  output Q2,
  output Q3,
  output Q4
);

  EdgeSRFlipFlop edgesrflipflop_1 (.CLK(CLK), .D(Q4), .S(R), .Q(Q1));  // open: qR, nQ
  EdgeSRFlipFlop edgesrflipflop_2 (.CLK(CLK), .D(Q1), .qR(R), .Q(Q2));  // open: S, nQ
  EdgeSRFlipFlop edgesrflipflop_3 (.CLK(CLK), .D(Q2), .qR(R), .Q(Q3));  // open: S, nQ
  EdgeSRFlipFlop edgesrflipflop_4 (.CLK(CLK), .D(Q3), .qR(R), .Q(Q4));  // open: S, nQ
endmodule

module Johnson2 (
  input  CLK,
  input  R,
  output Q1,
  output Q2
);

  wire edgesrflipflop_2_nq;

  EdgeSRFlipFlop edgesrflipflop_1 (.CLK(CLK), .D(edgesrflipflop_2_nq), .qR(R), .Q(Q1));  // open: S, nQ
  EdgeSRFlipFlop edgesrflipflop_2 (.CLK(CLK), .D(Q1), .qR(R), .Q(Q2), .nQ(edgesrflipflop_2_nq));  // open: S
endmodule

module Johnson4 (
  input  CLK,
  input  R,
  output Q1,
  output Q2,
  output Q3,
  output Q4
);

  wire edgesrflipflop_4_nq;

  EdgeSRFlipFlop edgesrflipflop_1 (.CLK(CLK), .D(edgesrflipflop_4_nq), .qR(R), .Q(Q1));  // open: S, nQ
  EdgeSRFlipFlop edgesrflipflop_2 (.CLK(CLK), .D(Q1), .qR(R), .Q(Q2));  // open: S, nQ
  EdgeSRFlipFlop edgesrflipflop_3 (.CLK(CLK), .D(Q2), .qR(R), .Q(Q3));  // open: S, nQ
  EdgeSRFlipFlop edgesrflipflop_4 (.CLK(CLK), .D(Q3), .qR(R), .Q(Q4), .nQ(edgesrflipflop_4_nq));  // open: S
endmodule

module Shifter_test (
  input  E,
  input  D,
  input  AS,
  input  S,
  input  R
);

  wire dflopflop_1_q, dflopflop_2_q, dflopflop_3_q, edgepcflipflop_1_q, edgepcflipflop_2_q,
       edgepcflipflop_3_q, edgesrflipflop_1_q, edgesrflipflop_2_q, edgesrflipflop_3_q, not_1_out, not_2_out,
       not_3_out, not_4_out, not_5_out, not_6_out, not_7_out, not_8_out, not_9_out, or_1_out, or_2_out,
       sflipflop_1_q, sflipflop_2_q, sflipflop_3_q;

  or or_1 (or_1_out, E, AS);
  or or_2 (or_2_out, D, AS);
  EdgeSRFlipFlop edgesrflipflop_1 (.CLK(or_1_out), .qR(R), .S(S), .Q(edgesrflipflop_1_q));  // open: D, nQ
  SFlipFlop sflipflop_1 (.S(S), .R(R), .D(or_2_out), .E(or_1_out), .Q(sflipflop_1_q));  // open: nQ
  not not_1 (not_1_out, or_1_out);
  EdgePCFlipFlop edgepcflipflop_1 (.R(R), .S(S), .D(or_2_out), .E(or_1_out), .Q(edgepcflipflop_1_q));  // open: nQ
  not not_2 (not_2_out, or_1_out);
  DFlopFlop dflopflop_1 (.S(S), .D(or_2_out), .CLK(or_1_out), .R(R), .Q(dflopflop_1_q));  // open: nQ
  not not_3 (not_3_out, or_1_out);
  EdgeSRFlipFlop edgesrflipflop_2 (
    .CLK(or_1_out), .D(edgesrflipflop_1_q), .qR(R), .S(S), .Q(edgesrflipflop_2_q));  // open: nQ
  EdgeSRFlipFlop edgesrflipflop_3 (
    .CLK(or_1_out), .D(edgesrflipflop_2_q), .qR(R), .S(S), .Q(edgesrflipflop_3_q));  // open: nQ
  SFlipFlop sflipflop_2 (.S(S), .R(R), .D(sflipflop_1_q), .E(not_1_out), .Q(sflipflop_2_q));  // open: nQ
  SFlipFlop sflipflop_3 (.S(S), .R(not_4_out), .D(sflipflop_2_q), .E(not_4_out), .Q(sflipflop_3_q));  // open: nQ
  not not_4 (not_4_out, not_1_out);
  EdgePCFlipFlop edgepcflipflop_2 (
    .R(R), .S(S), .D(edgepcflipflop_1_q), .E(not_2_out), .Q(edgepcflipflop_2_q));  // open: nQ
  EdgePCFlipFlop edgepcflipflop_3 (
    .R(R), .S(S), .D(edgepcflipflop_2_q), .E(not_5_out), .Q(edgepcflipflop_3_q));  // open: nQ
  not not_5 (not_5_out, not_2_out);
  DFlopFlop dflopflop_2 (.S(S), .D(dflopflop_1_q), .CLK(not_3_out), .R(R), .Q(dflopflop_2_q));  // open: nQ
  DFlopFlop dflopflop_3 (.S(S), .D(dflopflop_2_q), .CLK(not_6_out), .R(R), .Q(dflopflop_3_q));  // open: nQ
  not not_6 (not_6_out, not_3_out);
  EdgeSRFlipFlop edgesrflipflop_4 (.CLK(or_1_out), .D(edgesrflipflop_3_q), .qR(R), .S(S));  // open: Q, nQ
  SFlipFlop sflipflop_4 (.S(S), .R(R), .D(sflipflop_3_q), .E(not_7_out));  // open: Q, nQ
  not not_7 (not_7_out, not_4_out);
  EdgePCFlipFlop edgepcflipflop_4 (.R(R), .S(S), .D(edgepcflipflop_3_q), .E(not_8_out));  // open: Q, nQ
  not not_8 (not_8_out, not_5_out);
  DFlopFlop dflopflop_4 (.S(S), .D(dflopflop_3_q), .CLK(not_9_out), .R(R));  // open: Q, nQ
  not not_9 (not_9_out, not_6_out);
endmodule
