// Logisim project 4 ALU.circ as structural Verilog: 1 circuit, main circuit ALU
module ALU (
  input  [2:0] in_1,
  input  Cin,
  input  [3:0] A,
  input  [3:0] B,
  output [3:0] Z,
  output Cout
);

  wire demux8composed_1_y0, demux8composed_1_y1, demux8composed_1_y2, demux8composed_1_y3,
       demux8composed_1_y4, demux8composed_1_y5, demux8composed_1_y6, demux8composed_1_y7;
  wire [3:0] adder_1byte_1_s, and_4b_1_o, and_4b_2_o, and_4b_3_o, and_4b_4_o, and_4b_5_o, and_4b_6_o,
       and_4b_7_o, and_4b_8_o, subtractor_1byte_1_d;

  Adder_1byte adder_1byte_1 (.X(A), .Y(B), .Ci(Cin), .Co(Cout), .S(adder_1byte_1_s));
  Subtractor_1byte subtractor_1byte_1 (.X(A), .Y(B), .Bi(Cin), .D(subtractor_1byte_1_d), .Bo(Cout));
  Demux8composed demux8composed_1 (
    .S1(in_1[1]), .S0(in_1[0]), .D(1'b1), .S2(in_1[2]), .Y3(demux8composed_1_y3), .Y4(demux8composed_1_y4),
    .Y5(demux8composed_1_y5), .Y6(demux8composed_1_y6), .Y7(demux8composed_1_y7), .Y0(demux8composed_1_y0),
    .Y1(demux8composed_1_y1), .Y2(demux8composed_1_y2));
  And_4b and_4b_1 (.D(adder_1byte_1_s), .E(demux8composed_1_y0), .O(and_4b_1_o));
  And_4b and_4b_2 (.D(subtractor_1byte_1_d), .E(demux8composed_1_y1), .O(and_4b_2_o));
  And_4b and_4b_3 (.E(demux8composed_1_y2), .O(and_4b_3_o));  // open: D
  And_4b and_4b_4 (.E(demux8composed_1_y3), .O(and_4b_4_o));  // open: D
  And_4b and_4b_5 (.E(demux8composed_1_y4), .O(and_4b_5_o));  // open: D
  And_4b and_4b_6 (.E(demux8composed_1_y5), .O(and_4b_6_o));  // open: D
  And_4b and_4b_7 (.E(demux8composed_1_y6), .O(and_4b_7_o));  // open: D
  And_4b and_4b_8 (.E(demux8composed_1_y7), .O(and_4b_8_o));  // open: D
  assign Z = and_4b_1_o | and_4b_2_o | and_4b_3_o | and_4b_4_o | and_4b_5_o | and_4b_6_o | and_4b_7_o | and_4b_8_o;  // OR_Gate or_1, 4 bits wide
endmodule
