// Logisim project 4 RAM.circ as structural Verilog: 7 circuits, main circuit Reg1
module Reg1 (
  input  in_1,
  input  Read,
  input  D,
  input  Enable,
  input  Rst,
  output Q,
  output Qa
);

  wire dflopflop_1_q, not_1_out;

  DFlopFlop dflopflop_1 (.S(in_1), .D(D), .CLK(Enable), .R(Rst), .Q(dflopflop_1_q));  // open: nQ
  not not_1 (not_1_out, Enable);
  DFlopFlop dflopflop_2 (.S(in_1), .D(dflopflop_1_q), .CLK(not_1_out), .R(Rst), .Q(Qa));  // open: nQ
  LED led_1 (.in(dflopflop_1_q));
  and and_1 (Q, Read, Qa);
endmodule

module Reg4 (
  input  [3:0] Set,
  input  Read,
  input  Enable,
  input  Rst,
  input  [3:0] D,
  output [3:0] Q,
  output [3:0] Qa
);

  Reg1 reg1_1 (.in_1(Set[0]), .Read(Read), .D(D[0]), .Enable(Enable), .Rst(Rst), .Q(Q[0]), .Qa(Qa[0]));
  Reg1 reg1_2 (.in_1(Set[1]), .Read(Read), .D(D[1]), .Enable(Enable), .Rst(Rst), .Q(Q[1]), .Qa(Qa[1]));
  Reg1 reg1_3 (.in_1(Set[2]), .Read(Read), .D(D[2]), .Enable(Enable), .Rst(Rst), .Q(Q[2]), .Qa(Qa[2]));
  Reg1 reg1_4 (.in_1(Set[3]), .Read(Read), .D(D[3]), .Enable(Enable), .Rst(Rst), .Q(Q[3]), .Qa(Qa[3]));
  Hex_Digit_Display hex_digit_display_1 (.value(Qa));  // open: dp
endmodule

module Reg8 (
  input  [7:0] Set,
  input  Read,
  input  Enable,
  input  Rst,
  input  [7:0] D,
  output [7:0] Q,
  output [7:0] Qa
);

  Reg1 reg1_1 (.in_1(Set[0]), .Read(Read), .D(D[0]), .Enable(Enable), .Rst(Rst), .Q(Q[0]), .Qa(Qa[0]));
  Reg1 reg1_2 (.in_1(Set[1]), .Read(Read), .D(D[1]), .Enable(Enable), .Rst(Rst), .Q(Q[1]), .Qa(Qa[1]));
  Reg1 reg1_3 (.in_1(Set[2]), .Read(Read), .D(D[2]), .Enable(Enable), .Rst(Rst), .Q(Q[2]), .Qa(Qa[2]));
  Reg1 reg1_4 (.in_1(Set[3]), .Read(Read), .D(D[3]), .Enable(Enable), .Rst(Rst), .Q(Q[3]), .Qa(Qa[3]));
  Reg1 reg1_5 (.in_1(Set[4]), .Read(Read), .D(D[4]), .Enable(Enable), .Rst(Rst), .Q(Q[4]), .Qa(Qa[4]));
  Reg1 reg1_6 (.in_1(Set[5]), .Read(Read), .D(D[5]), .Enable(Enable), .Rst(Rst), .Q(Q[5]), .Qa(Qa[5]));
  Reg1 reg1_7 (.in_1(Set[6]), .Read(Read), .D(D[6]), .Enable(Enable), .Rst(Rst), .Q(Q[6]), .Qa(Qa[6]));
  Reg1 reg1_8 (.in_1(Set[7]), .Read(Read), .D(D[7]), .Enable(Enable), .Rst(Rst), .Q(Q[7]), .Qa(Qa[7]));
  Hex_Digit_Display hex_digit_display_1 (.value(Qa[7:4]));  // open: dp
  Hex_Digit_Display hex_digit_display_2 (.value(Qa[3:0]));  // open: dp
endmodule

module RAM16 (
  input  [3:0] Set,
  input  Read,
  input  [3:0] D,
  input  E,
  input  [3:0] Addr,
  input  Rst,
  output [3:0] Q
);

  wire and_1_out, and_2_out, and_3_out, and_4_out, and_5_out, and_6_out, and_7_out, and_8_out, and_9_out,
       and_10_out, and_11_out, and_12_out, and_13_out, and_14_out, and_15_out, and_16_out, demux4_1_y0,
       demux4_1_y1, demux4_1_y2, demux4_1_y3, demux4_2_y0, demux4_2_y1, demux4_2_y2, demux4_2_y3;
  wire [3:0] or_1_out, or_2_out, or_3_out, or_4_out, reg4_1_q, reg4_2_q, reg4_3_q, reg4_4_q, reg4_5_q,
       reg4_6_q, reg4_7_q, reg4_8_q, reg4_9_q, reg4_10_q, reg4_11_q, reg4_12_q, reg4_13_q, reg4_14_q,
       reg4_15_q, reg4_16_q;

  Demux4 demux4_1 (
    .S0(Addr[0]), .S1(Addr[1]), .D(E), .Y0(demux4_1_y0), .Y1(demux4_1_y1), .Y2(demux4_1_y2), .Y3(demux4_1_y3));
  Demux4 demux4_2 (
    .S0(Addr[2]), .S1(Addr[3]), .D(E), .Y0(demux4_2_y0), .Y1(demux4_2_y1), .Y2(demux4_2_y2), .Y3(demux4_2_y3));
  and and_1 (and_1_out, demux4_1_y0, demux4_2_y0);
  and and_2 (and_2_out, demux4_1_y0, demux4_2_y1);
  and and_3 (and_3_out, demux4_1_y0, demux4_2_y2);
  and and_4 (and_4_out, demux4_1_y0, demux4_2_y3);
  assign or_1_out = reg4_1_q | reg4_2_q | reg4_3_q | reg4_4_q;  // OR_Gate or_1, 4 bits wide
  Reg4 reg4_1 (.Set(Set), .Read(Read), .Enable(and_1_out), .Rst(Rst), .D(D), .Q(reg4_1_q));  // open: Qa
  Reg4 reg4_2 (.Read(Read), .Enable(and_2_out), .Rst(Rst), .D(D), .Q(reg4_2_q));  // open: Set, Qa
  Reg4 reg4_3 (.Read(Read), .Enable(and_3_out), .Rst(Rst), .D(D), .Q(reg4_3_q));  // open: Set, Qa
  Reg4 reg4_4 (.Read(Read), .Enable(and_4_out), .Rst(Rst), .D(D), .Q(reg4_4_q));  // open: Set, Qa
  and and_5 (and_5_out, demux4_1_y1, demux4_2_y0);
  and and_6 (and_6_out, demux4_1_y1, demux4_2_y1);
  and and_7 (and_7_out, demux4_1_y1, demux4_2_y2);
  and and_8 (and_8_out, demux4_1_y1, demux4_2_y3);
  assign or_2_out = reg4_5_q | reg4_6_q | reg4_7_q | reg4_8_q;  // OR_Gate or_2, 4 bits wide
  Reg4 reg4_5 (.Set(Set), .Read(Read), .Enable(and_5_out), .Rst(Rst), .D(D), .Q(reg4_5_q));  // open: Qa
  Reg4 reg4_6 (.Read(Read), .Enable(and_6_out), .Rst(Rst), .D(D), .Q(reg4_6_q));  // open: Set, Qa
  Reg4 reg4_7 (.Read(Read), .Enable(and_7_out), .Rst(Rst), .D(D), .Q(reg4_7_q));  // open: Set, Qa
  Reg4 reg4_8 (.Read(Read), .Enable(and_8_out), .Rst(Rst), .D(D), .Q(reg4_8_q));  // open: Set, Qa
  and and_9 (and_9_out, demux4_1_y2, demux4_2_y0);
  and and_10 (and_10_out, demux4_1_y2, demux4_2_y1);
  and and_11 (and_11_out, demux4_1_y2, demux4_2_y2);
  and and_12 (and_12_out, demux4_1_y2, demux4_2_y3);
  assign or_3_out = reg4_9_q | reg4_10_q | reg4_11_q | reg4_12_q;  // OR_Gate or_3, 4 bits wide
  Reg4 reg4_9 (.Set(Set), .Read(Read), .Enable(and_9_out), .Rst(Rst), .D(D), .Q(reg4_9_q));  // open: Qa
  Reg4 reg4_10 (.Read(Read), .Enable(and_10_out), .Rst(Rst), .D(D), .Q(reg4_10_q));  // open: Set, Qa
  Reg4 reg4_11 (.Read(Read), .Enable(and_11_out), .Rst(Rst), .D(D), .Q(reg4_11_q));  // open: Set, Qa
  Reg4 reg4_12 (.Read(Read), .Enable(and_12_out), .Rst(Rst), .D(D), .Q(reg4_12_q));  // open: Set, Qa
  and and_13 (and_13_out, demux4_1_y3, demux4_2_y0);
  and and_14 (and_14_out, demux4_1_y3, demux4_2_y1);
  and and_15 (and_15_out, demux4_1_y3, demux4_2_y2);
  and and_16 (and_16_out, demux4_1_y3, demux4_2_y3);
  assign or_4_out = reg4_13_q | reg4_14_q | reg4_15_q | reg4_16_q;  // OR_Gate or_4, 4 bits wide
  Reg4 reg4_13 (.Set(Set), .Read(Read), .Enable(and_13_out), .Rst(Rst), .D(D), .Q(reg4_13_q));  // open: Qa
  Reg4 reg4_14 (.Set(Set), .Read(Read), .Enable(and_14_out), .Rst(Rst), .D(D), .Q(reg4_14_q));  // open: Qa
  Reg4 reg4_15 (.Set(Set), .Read(Read), .Enable(and_15_out), .Rst(Rst), .D(D), .Q(reg4_15_q));  // open: Qa
  Reg4 reg4_16 (.Set(Set), .Read(Read), .Enable(and_16_out), .Rst(Rst), .D(D), .Q(reg4_16_q));  // open: Qa
  assign Q = or_1_out | or_2_out | or_3_out | or_4_out;  // OR_Gate or_5, 4 bits wide
endmodule

module PIPO_4bx12 (
  input  [3:0] D0,
  input  [3:0] D1,
  input  [3:0] D2,
  input  [3:0] D3,
  input  M0,
  input  M1,
  input  [3:0] SLI,
  input  [3:0] SRI,
  input  Read,
  input  [3:0] ASet,
  input  CLK,
  input  Rst,
  output [3:0] SLO,
  output [3:0] SRO,
  output [3:0] Q0,
  output [3:0] Q1,
  output [3:0] Q2,
  output [3:0] Q3
);

  wire [3:0] mux4_4b_1_y, mux4_4b_2_y, mux4_4b_3_y, mux4_4b_4_y, reg4_2_qa, reg4_3_qa;

  Mux4_4b mux4_4b_1 (.C(SLI), .D(D0), .S0(M0), .S1(M1), .A(SLO), .B(reg4_2_qa), .Y(mux4_4b_1_y));
  // Probe on mux4_4b_1_y
  Reg4 reg4_1 (.Set(ASet), .Read(Read), .Enable(CLK), .Rst(Rst), .D(mux4_4b_1_y), .Q(Q0), .Qa(SLO));
  Mux4_4b mux4_4b_2 (.C(SLO), .D(D1), .S0(M0), .S1(M1), .A(reg4_2_qa), .B(reg4_3_qa), .Y(mux4_4b_2_y));
  // Probe on mux4_4b_2_y
  Reg4 reg4_2 (.Set(ASet), .Read(Read), .Enable(CLK), .Rst(Rst), .D(mux4_4b_2_y), .Q(Q1), .Qa(reg4_2_qa));
  Mux4_4b mux4_4b_3 (.C(reg4_2_qa), .D(D2), .S0(M0), .S1(M1), .A(reg4_3_qa), .B(SRO), .Y(mux4_4b_3_y));
  // Probe on mux4_4b_3_y
  Reg4 reg4_3 (.Set(ASet), .Read(Read), .Enable(CLK), .Rst(Rst), .D(mux4_4b_3_y), .Q(Q2), .Qa(reg4_3_qa));
  Mux4_4b mux4_4b_4 (.C(reg4_3_qa), .D(D3), .S0(M0), .S1(M1), .A(SRO), .B(SRI), .Y(mux4_4b_4_y));
  // Probe on mux4_4b_4_y
  Reg4 reg4_4 (.Set(ASet), .Read(Read), .Enable(CLK), .Rst(Rst), .D(mux4_4b_4_y), .Q(Q3), .Qa(SRO));
endmodule

module PIPO_4b_unit (
  input  [3:0] D0,
  input  M0,
  input  M1,
  input  [3:0] SLI,
  input  [3:0] SRI,
  input  Read,
  input  [3:0] ASet,
  input  CLK,
  input  Rst,
  output [3:0] SLO,
  output [3:0] SRO,
  output [3:0] Q0
);

  wire [3:0] mux4_4b_1_y;

  Mux4_4b mux4_4b_1 (.C(SLI), .D(D0), .S0(M0), .S1(M1), .A(SLO), .B(SRI), .Y(mux4_4b_1_y));
  // Probe on mux4_4b_1_y
  Reg4 reg4_1 (.Set(ASet), .Read(Read), .Enable(CLK), .Rst(Rst), .D(mux4_4b_1_y), .Q(Q0), .Qa(SLO));

  assign SRO = SLO;
endmodule

module PIPO_4b_12 (
  input  [3:0] D0,
  input  [3:0] D1,
  input  [3:0] D2,
  input  [3:0] D3,
  input  [3:0] D4,
  input  [3:0] D5,
  input  [3:0] D6,
  input  [3:0] D7,
  input  [3:0] D8,
  input  [3:0] D9,
  input  [3:0] D10,
  input  [3:0] D11,
  input  M0,
  input  M1,
  input  Read,
  input  CLK,
  input  [3:0] SLI,
  input  [3:0] SRI,
  input  Rst,
  input  [3:0] ASet,
  output [3:0] SLO,
  output [3:0] SRO,
  output [3:0] Q0,
  output [3:0] Q1,
  output [3:0] Q2,
  output [3:0] Q3,
  output [3:0] Q4,
  output [3:0] Q5,
  output [3:0] Q6,
  output [3:0] Q7,
  output [3:0] Q8,
  output [3:0] Q9,
  output [3:0] Q10,
  output [3:0] Q11
);

  wire [3:0] pipo_4b_unit_1_sro, pipo_4b_unit_2_slo, pipo_4b_unit_2_sro, pipo_4b_unit_3_slo,
       pipo_4b_unit_3_sro, pipo_4b_unit_4_slo, pipo_4b_unit_4_sro, pipo_4b_unit_5_slo, pipo_4b_unit_5_sro,
       pipo_4b_unit_6_slo, pipo_4b_unit_6_sro, pipo_4b_unit_7_slo, pipo_4b_unit_7_sro, pipo_4b_unit_8_slo,
       pipo_4b_unit_8_sro, pipo_4b_unit_9_slo, pipo_4b_unit_9_sro, pipo_4b_unit_10_slo, pipo_4b_unit_10_sro,
       pipo_4b_unit_11_slo, pipo_4b_unit_11_sro, pipo_4b_unit_12_slo;

  PIPO_4b_unit pipo_4b_unit_1 (
    .M0(M0), .M1(M1), .SLI(SLI), .Read(Read), .ASet(ASet), .CLK(CLK), .Rst(Rst), .D0(D0),
    .SRI(pipo_4b_unit_2_slo), .SLO(SLO), .Q0(Q0), .SRO(pipo_4b_unit_1_sro));
  PIPO_4b_unit pipo_4b_unit_2 (
    .M0(M0), .M1(M1), .SLI(pipo_4b_unit_1_sro), .Read(Read), .ASet(ASet), .CLK(CLK), .Rst(Rst), .D0(D1),
    .SRI(pipo_4b_unit_3_slo), .SLO(pipo_4b_unit_2_slo), .Q0(Q1), .SRO(pipo_4b_unit_2_sro));
  PIPO_4b_unit pipo_4b_unit_3 (
    .M0(M0), .M1(M1), .SLI(pipo_4b_unit_2_sro), .Read(Read), .ASet(ASet), .CLK(CLK), .Rst(Rst), .D0(D2),
    .SRI(pipo_4b_unit_4_slo), .SLO(pipo_4b_unit_3_slo), .Q0(Q2), .SRO(pipo_4b_unit_3_sro));
  PIPO_4b_unit pipo_4b_unit_4 (
    .M0(M0), .M1(M1), .SLI(pipo_4b_unit_3_sro), .Read(Read), .ASet(ASet), .CLK(CLK), .Rst(Rst), .D0(D3),
    .SRI(pipo_4b_unit_5_slo), .SLO(pipo_4b_unit_4_slo), .Q0(Q3), .SRO(pipo_4b_unit_4_sro));
  PIPO_4b_unit pipo_4b_unit_5 (
    .M0(M0), .M1(M1), .SLI(pipo_4b_unit_4_sro), .Read(Read), .ASet(ASet), .CLK(CLK), .Rst(Rst), .D0(D4),
    .SRI(pipo_4b_unit_6_slo), .SLO(pipo_4b_unit_5_slo), .Q0(Q4), .SRO(pipo_4b_unit_5_sro));
  PIPO_4b_unit pipo_4b_unit_6 (
    .M0(M0), .M1(M1), .SLI(pipo_4b_unit_5_sro), .Read(Read), .ASet(ASet), .CLK(CLK), .Rst(Rst), .D0(D5),
    .SRI(pipo_4b_unit_7_slo), .SLO(pipo_4b_unit_6_slo), .Q0(Q5), .SRO(pipo_4b_unit_6_sro));
  PIPO_4b_unit pipo_4b_unit_7 (
    .M0(M0), .M1(M1), .SLI(pipo_4b_unit_6_sro), .Read(Read), .ASet(ASet), .CLK(CLK), .Rst(Rst), .D0(D6),
    .SRI(pipo_4b_unit_8_slo), .SLO(pipo_4b_unit_7_slo), .Q0(Q6), .SRO(pipo_4b_unit_7_sro));
  PIPO_4b_unit pipo_4b_unit_8 (
    .M0(M0), .M1(M1), .SLI(pipo_4b_unit_7_sro), .Read(Read), .ASet(ASet), .CLK(CLK), .Rst(Rst), .D0(D7),
    .SRI(pipo_4b_unit_9_slo), .SLO(pipo_4b_unit_8_slo), .Q0(Q7), .SRO(pipo_4b_unit_8_sro));
  PIPO_4b_unit pipo_4b_unit_9 (
    .M0(M0), .M1(M1), .SLI(pipo_4b_unit_8_sro), .Read(Read), .ASet(ASet), .CLK(CLK), .Rst(Rst), .D0(D8),
    .SRI(pipo_4b_unit_10_slo), .SLO(pipo_4b_unit_9_slo), .Q0(Q8), .SRO(pipo_4b_unit_9_sro));
  PIPO_4b_unit pipo_4b_unit_10 (
    .M0(M0), .M1(M1), .SLI(pipo_4b_unit_9_sro), .Read(Read), .ASet(ASet), .CLK(CLK), .Rst(Rst), .D0(D9),
    .SRI(pipo_4b_unit_11_slo), .SLO(pipo_4b_unit_10_slo), .Q0(Q9), .SRO(pipo_4b_unit_10_sro));
  PIPO_4b_unit pipo_4b_unit_11 (
    .M0(M0), .M1(M1), .SLI(pipo_4b_unit_10_sro), .Read(Read), .ASet(ASet), .CLK(CLK), .Rst(Rst), .D0(D10),
    .SRI(pipo_4b_unit_12_slo), .SLO(pipo_4b_unit_11_slo), .Q0(Q10), .SRO(pipo_4b_unit_11_sro));
  PIPO_4b_unit pipo_4b_unit_12 (
    .M0(M0), .M1(M1), .SLI(pipo_4b_unit_11_sro), .Read(Read), .ASet(ASet), .CLK(CLK), .Rst(Rst), .D0(D11),
    .SRI(SRI), .SLO(pipo_4b_unit_12_slo), .Q0(Q11), .SRO(SRO));
endmodule
