// Logisim project 5 CPU.circ as structural Verilog: 1 circuit, main circuit main
module main (
);

  wire add_out, and_1_out, and_2_out, b0_out, b1_out, b2_out, b3_out, b4_out, b5_out, b6_out, b7_out, b8_out,
       b9_out, bcd_kbrd_byte_1_a, C_out, clock_1_out, div_out, eq_out, mul_out, or_1_out, or_2_out,
       ring4_1_q2, ring4_1_q3, RST_out, sub_out;
  wire [3:0] bcd_kbrd_byte_1_q, pipo_4b_12_2_q0, pipo_4b_12_2_q1, pipo_4b_12_2_q2, pipo_4b_12_2_q3,
       pipo_4b_12_2_q4, pipo_4b_12_2_q5, pipo_4b_12_2_q6, pipo_4b_12_2_q7, pipo_4b_12_2_q8, pipo_4b_12_2_q9,
       pipo_4b_12_2_q10, pipo_4b_12_2_q11, pipo_4b_12_2_slo;

  Button C (.out(C_out));
  Button RST (.out(RST_out));
  Button b1 (.out(b1_out));
  Button b2 (.out(b2_out));
  Button b3 (.out(b3_out));
  Button b0 (.out(b0_out));
  Button add (.out(add_out));
  Button sub (.out(sub_out));
  Button b4 (.out(b4_out));
  Button b5 (.out(b5_out));
  Button b6 (.out(b6_out));
  Button b7 (.out(b7_out));
  Button mul (.out(mul_out));
  Button div (.out(div_out));
  Button eq (.out(eq_out));
  Ring4 ring4_1 (.CLK(clock_1_out), .R(or_2_out), .Q2(ring4_1_q2), .Q3(ring4_1_q3));  // open: Q1, Q4
  Clock clock_1 (.out(clock_1_out));
  Button b8 (.out(b8_out));
  Button b9 (.out(b9_out));
  BCD_KBRD_byte bcd_kbrd_byte_1 (
    .I4(b4_out), .I5(b5_out), .I6(b6_out), .I7(b7_out), .I8(b8_out), .I9(b9_out), .I0(b0_out), .I1(b1_out),
    .I2(b2_out), .I3(b3_out), .A(bcd_kbrd_byte_1_a), .Q(bcd_kbrd_byte_1_q));
  and and_1 (and_1_out, ring4_1_q2, or_2_out);
  and and_2 (and_2_out, ring4_1_q3, or_2_out);
  PIPO_4b_12 pipo_4b_12_1 (
    .D10(pipo_4b_12_2_q10), .D11(pipo_4b_12_2_q11), .M0(and_1_out), .M1(and_1_out), .CLK(and_1_out),
    .SLI(pipo_4b_12_2_slo), .Rst(RST_out), .D0(pipo_4b_12_2_q0), .D1(pipo_4b_12_2_q1), .D2(pipo_4b_12_2_q2),
    .D3(pipo_4b_12_2_q3), .D4(pipo_4b_12_2_q4), .D5(pipo_4b_12_2_q5), .D6(pipo_4b_12_2_q6),
    .D7(pipo_4b_12_2_q7), .D8(pipo_4b_12_2_q8), .D9(pipo_4b_12_2_q9));  // open: Read, ASet, SRI, Q9, Q10, Q11, SLO, SRO, Q0, Q1, Q2, Q3, Q4, Q5, Q6, Q7, Q8
  PIPO_4b_12 pipo_4b_12_2 (
    .M0(1'b0), .M1(bcd_kbrd_byte_1_a), .Read(or_2_out), .CLK(bcd_kbrd_byte_1_a), .SLI(bcd_kbrd_byte_1_q),
    .Rst(or_1_out), .Q9(pipo_4b_12_2_q9), .Q10(pipo_4b_12_2_q10), .Q11(pipo_4b_12_2_q11),
    .SLO(pipo_4b_12_2_slo), .Q0(pipo_4b_12_2_q0), .Q1(pipo_4b_12_2_q1), .Q2(pipo_4b_12_2_q2),
    .Q3(pipo_4b_12_2_q3), .Q4(pipo_4b_12_2_q4), .Q5(pipo_4b_12_2_q5), .Q6(pipo_4b_12_2_q6),
    .Q7(pipo_4b_12_2_q7), .Q8(pipo_4b_12_2_q8));  // open: D10, D11, ASet, SRI, D0, D1, D2, D3, D4, D5, D6, D7, D8, D9, SRO
  or or_1 (or_1_out, RST_out, and_2_out, C_out);
  or or_2 (or_2_out, eq_out, div_out, mul_out, sub_out, add_out);

  // Notes on the sheet:
  //   RegB
  //   RegA
  //   put ALU here
endmodule
