// Logisim project Calculator.circ as structural Verilog: 16 circuits, main circuit main
module main (
);

  wire clock_1_out, I0_out, I1_out, I2_out, I3_out, I4_out, I5_out, I6_out, I7_out, I8_out, I9_out,
       kbrd_byte_1_a, mem_1_q, undriven, undriven_2, undriven_3, undriven_4;
  wire [3:0] bcd_byte_1_q, bcd_byte_2_q, bcd_byte_3_q, bcd_byte_4_q, kbrd_byte_1_q, mux_21_byte_1_q,
       mux_21_byte_2_q, mux_21_byte_3_q, undriven_5;

  LED_byte led_byte_1 (.D(bcd_byte_1_q), .dp(undriven_2));
  LED_byte led_byte_2 (.D(bcd_byte_2_q), .dp(undriven_2));
  BCD_byte bcd_byte_1 (.WE(undriven), .RST(undriven_4), .CLK(undriven_3), .D(mux_21_byte_1_q), .Q(bcd_byte_1_q));
  MUX_21_byte mux_21_byte_1 (.D0(bcd_byte_2_q), .D1(undriven_5), .S(undriven), .Q(mux_21_byte_1_q));
  Button I7 (.out(I7_out));
  Button I4 (.out(I4_out));
  Button I1 (.out(I1_out));
  Button I0 (.out(I0_out));
  BCD_byte bcd_byte_2 (.WE(undriven), .RST(undriven_4), .CLK(undriven_3), .D(mux_21_byte_2_q), .Q(bcd_byte_2_q));
  MUX_21_byte mux_21_byte_2 (.D0(bcd_byte_3_q), .D1(undriven_5), .S(undriven), .Q(mux_21_byte_2_q));
  Button I8 (.out(I8_out));
  Button I5 (.out(I5_out));
  Button I2 (.out(I2_out));
  Button dot ();  // open: out
  LED_byte led_byte_3 (.D(bcd_byte_3_q), .dp(undriven_2));
  BCD_byte bcd_byte_3 (.WE(undriven), .RST(undriven_4), .CLK(undriven_3), .D(mux_21_byte_3_q), .Q(bcd_byte_3_q));
  MUX_21_byte mux_21_byte_3 (.D0(bcd_byte_4_q), .D1(undriven_5), .S(undriven), .Q(mux_21_byte_3_q));
  Button I9 (.out(I9_out));
  Button I6 (.out(I6_out));
  Button I3 (.out(I3_out));
  Button eq ();  // open: out
  LED_byte led_byte_4 (.D(bcd_byte_4_q), .dp(undriven_2));
  BCD_byte bcd_byte_4 (.WE(undriven), .RST(undriven_4), .CLK(undriven_3), .D(undriven_5), .Q(bcd_byte_4_q));
  KBRD_byte kbrd_byte_1 (
    .I4(I4_out), .I5(I5_out), .I6(I6_out), .I7(I7_out), .I8(I8_out), .I9(I9_out), .I0(I0_out), .I1(I1_out),
    .I2(I2_out), .I3(I3_out), .A(kbrd_byte_1_a), .Q(kbrd_byte_1_q));
  Button div ();  // open: out
  Button mul ();  // open: out
  Button sub ();  // open: out
  Button plus ();  // open: out
  Button E ();  // open: out
  Clock clock_1 (.out(clock_1_out));
  MEM mem_1 (.D(I9_out), .CLK(clock_1_out), .RST(1'b0), .Q(mem_1_q));  // open: WR
  MEM mem_2 (.D(mem_1_q), .CLK(clock_1_out), .RST(1'b0));  // open: WR, Q
endmodule

module BCD_HEX_LED (
  input  Idp,
  input  iA,
  input  iB,
  input  iC,
  input  iD
);

  wire A_B_out, A_C_out, A_D_out, A_nB_nC_out, A_nB_out, A_nC_D_out, A_nC_out, A_nD_out, B_C_nD_out, B_C_out,
       B_nC_D_out, B_nD_out, C_nD_out, nA_B_D_out, nA_B_nC_out, nA_B_out, nA_C_D_out, nA_C_out, nA_D_out,
       nA_nB_nD_out, nA_nC_nD_out, nA_nC_out, nB_C_D_out, nB_C_out, nB_nC_out, nB_nD_out, nC_D_out,
       nC_nD_out, not_1_out, not_2_out, not_3_out, not_4_out, or_1_out, or_2_out, or_3_out, or_4_out,
       or_5_out, or_6_out, or_7_out;

  not not_1 (not_1_out, iA);
  not not_2 (not_2_out, iB);
  not not_3 (not_3_out, iC);
  not not_4 (not_4_out, iD);
  and A_nB_nC (A_nB_nC_out, iA, not_2_out, not_3_out);
  and nA_B_D (nA_B_D_out, not_1_out, iB, iD);
  and A_nD (A_nD_out, iA, not_4_out);
  and nA_C (nA_C_out, not_1_out, iC);
  and B_C (B_C_out, iB, iC);
  and nB_nD (nB_nD_out, not_2_out, not_4_out);
  and nA_nC_nD (nA_nC_nD_out, not_1_out, not_3_out, not_4_out);
  and nA_C_D (nA_C_D_out, not_1_out, iC, iD);
  and A_nC_D (A_nC_D_out, iA, not_3_out, iD);
  and nB_nC (nB_nC_out, not_2_out, not_3_out);
  and nA_nC (nA_nC_out, not_1_out, not_3_out);
  and nA_D (nA_D_out, not_1_out, iD);
  and nC_D (nC_D_out, not_3_out, iD);
  and nA_B (nA_B_out, not_1_out, iB);
  and A_nB (A_nB_out, iA, not_2_out);
  and nA_nB_nD (nA_nB_nD_out, not_1_out, not_2_out, not_4_out);
  and nB_C_D (nB_C_D_out, not_2_out, iC, iD);
  and B_nC_D (B_nC_D_out, iB, not_3_out, iD);
  and B_C_nD (B_C_nD_out, iB, iC, not_4_out);
  and A_nC (A_nC_out, iA, not_3_out);
  and C_nD (C_nD_out, iC, not_4_out);
  and A_C (A_C_out, iA, iC);
  and A_B (A_B_out, iA, iB);
  and nA_B_nC (nA_B_nC_out, not_1_out, iB, not_3_out);
  and nC_nD (nC_nD_out, not_3_out, not_4_out);
  and B_nD (B_nD_out, iB, not_4_out);
  and nB_C (nB_C_out, not_2_out, iC);
  and A_D (A_D_out, iA, iD);
  or or_1 (or_1_out, A_nB_nC_out, nA_B_D_out, A_nD_out, nA_C_out, B_C_out, nB_nD_out);
  or or_2 (or_2_out, nA_nC_nD_out, nA_C_D_out, A_nC_D_out, nB_nD_out, nB_nC_out);
  or or_3 (or_3_out, nA_nC_out, nA_D_out, nC_D_out, nA_B_out, A_nB_out);
  or or_4 (or_4_out, nA_nB_nD_out, nB_C_D_out, B_nC_D_out, B_C_nD_out, A_nC_out);
  HEX_LED hex_led_1 (
    .a(or_1_out), .b(or_2_out), .c(or_3_out), .d(or_4_out), .e(or_5_out), .f(or_6_out), .g(or_7_out), .dp(Idp));
  or or_5 (or_5_out, nB_nD_out, C_nD_out, A_C_out, A_B_out);
  or or_6 (or_6_out, A_nB_out, A_C_out, nA_B_nC_out, nC_nD_out, B_nD_out);
  or or_7 (or_7_out, A_nB_out, C_nD_out, nA_B_nC_out, nB_C_out, A_D_out);
endmodule

module HEX_LED (
  input  a,
  input  b,
  input  c,
  input  d,
  input  e,
  input  f,
  input  g,
  input  dp
);

  _7_Segment_Display O (.g(g), .f(f), .a(a), .b(b), .e(e), .d(d), .c(c), .dp(dp));
endmodule

module KBRD (
  input  I0,
  input  I1,
  input  I2,
  input  I3,
  input  I4,
  input  I5,
  input  I6,
  input  I7,
  input  I8,
  input  I9,
  output O0,
  output O1,
  output O2,
  output O3,
  output A
);

  or or_1 (O0, I1, I3, I5, I7, I9);
  or or_2 (O1, I2, I3, I6, I7);
  or or_3 (O2, I4, I5, I6, I7);
  or or_4 (O3, I8, I9);
  or or_5 (A, I9, I8, I7, I6, I5, I4, I3, I2, I1, I0);
  Hex_Digit_Display hex_digit_display_1 (.value({O3, O2, O1, O0}));  // open: dp
  LED led_1 (.in(A));
endmodule

module BIN_ADDER (
  input  A,
  input  B,
  input  S,
  input  Cout,
  input  Cin
);

  wire and_1_out, and_2_out, xor_1_out;

  xor xor_1 (xor_1_out, A, B);
  and and_1 (and_1_out, A, B);
  xor xor_2 (S, xor_1_out, Cin);
  or or_1 (Cout, and_1_out, and_2_out);
  and and_2 (and_2_out, xor_1_out, Cin);
endmodule

module DLatch (
  input  D,
  input  CLK,
  output Q
);

  wire nand_1_out, nand_2_out, not_1_out;

  not not_1 (not_1_out, D);
  nand nand_1 (nand_1_out, D, CLK);
  SRLatch srlatch_1 (.R(nand_2_out), .S(nand_1_out), .Q(Q));  // open: nQ
  nand nand_2 (nand_2_out, not_1_out, CLK);
  LED led_1 (.in(Q));
endmodule

module BCD (
  input  D0,
  input  D1,
  input  D2,
  input  D3,
  input  WE,
  input  CLK,
  input  RST,
  output Q0,
  output Q1,
  output Q2,
  output Q3
);

  RegLatch reglatch_1 (.RST(RST), .D(D0), .E(WE), .CLK(CLK), .Q(Q0));
  RegLatch reglatch_2 (.RST(RST), .D(D1), .E(WE), .CLK(CLK), .Q(Q1));
  RegLatch reglatch_3 (.RST(RST), .D(D2), .E(WE), .CLK(CLK), .Q(Q2));
  RegLatch reglatch_4 (.RST(RST), .D(D3), .E(WE), .CLK(CLK), .Q(Q3));
  Hex_Digit_Display hex_digit_display_1 (.value({Q3, Q2, Q1, Q0}));  // open: dp
endmodule

module MEM (
  input  D,
  input  WR,
  input  CLK,
  input  RST,
  output Q
);

  wire and_1_out, and_2_out, not_1_out, not_2_out;

  and and_1 (and_1_out, WR, not_1_out);
  not not_1 (not_1_out, CLK);
  DLatch dlatch_1 (.D(D), .CLK(and_1_out), .Q(Q));
  not not_2 (not_2_out, not_1_out);
  and and_2 (and_2_out, WR, not_2_out);
  DLatch dlatch_2 (.D(D), .CLK(and_2_out), .Q(Q));
  LED led_1 (.in(Q));
endmodule

module BCD_byte (
  input  CLK,
  input  [3:0] D,
  input  WE,
  input  RST,
  output [3:0] Q
);

  BCD bcd_1 (
    .D1(D[1]), .D2(D[2]), .D3(D[3]), .WE(WE), .CLK(CLK), .RST(RST), .D0(D[0]), .Q1(Q[1]), .Q2(Q[2]),
    .Q3(Q[3]), .Q0(Q[0]));
  Hex_Digit_Display hex_digit_display_1 (.value(Q));  // open: dp
endmodule

module KBRD_byte (
  input  I0,
  input  I1,
  input  I2,
  input  I3,
  input  I4,
  input  I5,
  input  I6,
  input  I7,
  input  I8,
  input  I9,
  output [3:0] Q,
  output A
);

  KBRD kbrd_1 (
    .I1(I1), .I2(I2), .I3(I3), .I4(I4), .I5(I5), .I6(I6), .I7(I7), .I8(I8), .I9(I9), .I0(I0), .O0(Q[0]),
    .O1(Q[1]), .O2(Q[2]), .O3(Q[3]), .A(A));
  Hex_Digit_Display hex_digit_display_1 (.value(Q));  // open: dp
endmodule

module LED_byte (
  input  [3:0] D,
  input  dp
);

  Hex_Digit_Display hex_digit_display_1 (.value(D));  // open: dp
  BCD_HEX_LED bcd_hex_led_1 (.Idp(dp), .iA(D[0]), .iB(D[1]), .iC(D[2]), .iD(D[3]));
endmodule

module MUX_21 (
  input  S,
  input  D0,
  input  D1,
  output Y
);

  wire and_1_out, and_2_out, not_1_out;

  not not_1 (not_1_out, S);
  LED led_1 (.in(and_1_out));
  and and_1 (and_1_out, not_1_out, D0);
  and and_2 (and_2_out, S, D1);
  LED led_2 (.in(and_2_out));
  or or_1 (Y, and_1_out, and_2_out);
endmodule

module MUX_21_byte (
  input  [3:0] D0,
  input  [3:0] D1,
  input  S,
  output [3:0] Q
);

  wire and_1_out, and_2_out, not_1_out, or_1_out, or_2_out;

  or or_1 (or_1_out, D1[3], D1[2], D1[1], D1[0]);
  and and_1 (and_1_out, or_1_out, S);
  LED led_1 (.in(and_1_out));
  not not_1 (not_1_out, S);
  or or_2 (or_2_out, D0[3], D0[2], D0[1], D0[0]);
  and and_2 (and_2_out, or_2_out, not_1_out);
  LED led_2 (.in(and_2_out));
  MUX_21 mux_21_1 (.D0(D0[0]), .D1(D1[0]), .S(S), .Y(Q[0]));
  MUX_21 mux_21_2 (.D0(D0[1]), .D1(D1[1]), .S(S), .Y(Q[1]));
  MUX_21 mux_21_3 (.D0(D0[2]), .D1(D1[2]), .S(S), .Y(Q[2]));
  MUX_21 mux_21_4 (.D0(D0[3]), .D1(D1[3]), .S(S), .Y(Q[3]));
endmodule

module SRLatch (
  input  S,
  input  R,
  output Q,
  output nQ
);

  nand nand_1 (Q, S, nQ);
  LED led_1 (.in(Q));
  nand nand_2 (nQ, Q, R);
endmodule

module DFlipFlop (
  input  D,
  input  CLK,
  output Q
);

  wire dlatch_1_q, not_1_out;

  DLatch dlatch_1 (.D(D), .CLK(CLK), .Q(dlatch_1_q));
  DLatch dlatch_2 (.D(dlatch_1_q), .CLK(not_1_out), .Q(Q));
  LED led_1 (.in(Q));
  not not_1 (not_1_out, CLK);
endmodule

module RegLatch (
  input  RST,
  input  D,
  input  E,
  input  CLK,
  output Q
);

  wire and_1_out, and_2_out, not_1_out, or_1_out;

  not not_1 (not_1_out, RST);
  and and_1 (and_1_out, E, CLK);
  and and_2 (and_2_out, not_1_out, D);
  DFlipFlop dflipflop_1 (.D(and_2_out), .CLK(or_1_out), .Q(Q));
  or or_1 (or_1_out, RST, and_1_out);
  LED led_1 (.in(Q));
endmodule
