// Logisim project RCA_CMOS.circ as structural Verilog: 4 circuits, main circuit CD4000B
module CD4000A (
  input  Vdd,
  input  C,
  input  D,
  input  A,
  input  E,
  input  B,
  input  F,
  input  G,
  output Vss,
  output H,
  output L,
  output K
);

  wire transistor_2_out, transistor_3_out, transistor_9_out, transistor_10_out, transistor_12_out;

  Transistor #(.\type ("n")) transistor_1 (.in(1'b0), .out(H), .gate(C));
  Transistor transistor_2 (.in(Vdd), .out(transistor_2_out), .gate(C));
  Transistor transistor_3 (.in(transistor_2_out), .out(transistor_3_out), .gate(A));
  Transistor transistor_4 (.in(transistor_3_out), .out(H), .gate(B));
  Transistor #(.\type ("n")) transistor_5 (.in(1'b0), .out(H), .gate(A));
  Transistor #(.\type ("n")) transistor_6 (.in(1'b0), .out(H), .gate(B));
  Transistor transistor_7 (.in(Vdd), .out(L), .gate(G));
  Transistor #(.\type ("n")) transistor_8 (.in(1'b0), .out(L), .gate(G));
  Transistor transistor_9 (.in(Vdd), .out(transistor_9_out), .gate(D));
  Transistor transistor_10 (.in(transistor_9_out), .out(transistor_10_out), .gate(E));
  Transistor transistor_11 (.in(transistor_10_out), .out(K), .gate(F));
  Transistor #(.\type ("n")) transistor_12 (.in(1'b0), .out(transistor_12_out), .gate(F));
  Transistor #(.\type ("n")) transistor_13 (.in(1'b0), .out(transistor_12_out), .gate(E));
  Transistor #(.\type ("n")) transistor_14 (.in(1'b0), .out(transistor_12_out), .gate(D));

  assign Vss = 1'b0;
  // also tied to VCC on the sheet: Vdd
endmodule

module CD4000B (
  input  Vdd,
  input  G,
  input  C,
  input  E,
  input  A,
  input  D,
  input  B,
  input  F,
  output H,
  output K,
  output L,
  output Vss
);

  wire transistor_1_out, transistor_2_out, transistor_5_out, transistor_9_out, transistor_10_out,
       transistor_11_out, transistor_15_out, transistor_17_out, transistor_19_out, transistor_23_out,
       transistor_24_out, transistor_25_out, transistor_29_out, transistor_31_out;

  Transistor transistor_1 (.in(Vdd), .out(transistor_1_out), .gate(transistor_2_out));
  Transistor transistor_2 (.in(Vdd), .out(transistor_2_out), .gate(C));
  Transistor #(.\type ("n")) transistor_3 (.in(1'b0), .out(transistor_2_out), .gate(C));
  Transistor transistor_4 (.in(Vdd), .out(transistor_1_out), .gate(transistor_5_out));
  Transistor transistor_5 (.in(Vdd), .out(transistor_5_out), .gate(A));
  Transistor #(.\type ("n")) transistor_6 (.in(1'b0), .out(transistor_5_out), .gate(A));
  Transistor transistor_7 (.in(Vdd), .out(transistor_1_out), .gate(transistor_10_out));
  Transistor #(.\type ("n")) transistor_8 (.in(transistor_9_out), .out(transistor_1_out), .gate(transistor_2_out));
  Transistor #(.\type ("n")) transistor_9 (.in(transistor_11_out), .out(transistor_9_out), .gate(transistor_5_out));
  Transistor transistor_10 (.in(Vdd), .out(transistor_10_out), .gate(B));
  Transistor #(.\type ("n")) transistor_11 (.in(1'b0), .out(transistor_11_out), .gate(transistor_10_out));
  Transistor #(.\type ("n")) transistor_12 (.in(1'b0), .out(transistor_10_out), .gate(B));
  Transistor transistor_13 (.in(Vdd), .out(H), .gate(transistor_1_out));
  Transistor #(.\type ("n")) transistor_14 (.in(1'b0), .out(H), .gate(transistor_1_out));
  Transistor transistor_15 (.in(Vdd), .out(transistor_15_out), .gate(E));
  Transistor #(.\type ("n")) transistor_16 (.in(1'b0), .out(transistor_15_out), .gate(E));
  Transistor transistor_17 (.in(Vdd), .out(transistor_17_out), .gate(transistor_15_out));
  Transistor transistor_18 (.in(Vdd), .out(transistor_17_out), .gate(transistor_19_out));
  Transistor transistor_19 (.in(Vdd), .out(transistor_19_out), .gate(D));
  Transistor #(.\type ("n")) transistor_20 (.in(1'b0), .out(transistor_19_out), .gate(D));
  Transistor transistor_21 (.in(Vdd), .out(transistor_17_out), .gate(transistor_24_out));
  Transistor #(.\type ("n")) transistor_22 (.in(transistor_23_out), .out(transistor_17_out), .gate(transistor_15_out));
  Transistor #(.\type ("n")) transistor_23 (.in(transistor_25_out), .out(transistor_23_out), .gate(transistor_19_out));
  Transistor transistor_24 (.in(Vdd), .out(transistor_24_out), .gate(F));
  Transistor #(.\type ("n")) transistor_25 (.in(1'b0), .out(transistor_25_out), .gate(transistor_24_out));
  Transistor #(.\type ("n")) transistor_26 (.in(1'b0), .out(transistor_24_out), .gate(F));
  Transistor transistor_27 (.in(Vdd), .out(K), .gate(transistor_17_out));
  Transistor #(.\type ("n")) transistor_28 (.in(1'b0), .out(K), .gate(transistor_17_out));
  Transistor transistor_29 (.in(Vdd), .out(transistor_29_out), .gate(G));
  Transistor #(.\type ("n")) transistor_30 (.in(1'b0), .out(transistor_29_out), .gate(G));
  Transistor transistor_31 (.in(Vdd), .out(transistor_31_out), .gate(transistor_29_out));
  Transistor #(.\type ("n")) transistor_32 (.in(1'b0), .out(transistor_31_out), .gate(transistor_29_out));
  Transistor transistor_33 (.in(Vdd), .out(L), .gate(transistor_31_out));
  Transistor #(.\type ("n")) transistor_34 (.in(1'b0), .out(L), .gate(transistor_31_out));

  assign Vss = 1'b0;
  // also tied to VCC on the sheet: Vdd
endmodule

module CD4001B (
  input  Vdd,
  input  A,
  input  D,
  input  B,
  input  C,
  input  E,
  input  H,
  input  F,
  input  G,
  output J,
  output K,
  output L,
  output M,
  output Vss
);

  wire transistor_1_out, transistor_3_out, transistor_5_out, transistor_6_out, transistor_8_out,
       transistor_9_out, transistor_15_out, transistor_20_out, transistor_21_out, transistor_22_out,
       transistor_24_out, transistor_26_out, transistor_27_out, transistor_29_out, transistor_33_out,
       transistor_36_out;

  Transistor transistor_1 (.in(Vdd), .out(transistor_1_out), .gate(A));
  Transistor #(.\type ("n")) transistor_2 (.in(1'b0), .out(transistor_1_out), .gate(A));
  Transistor transistor_3 (.in(Vdd), .out(transistor_3_out), .gate(E));
  Transistor #(.\type ("n")) transistor_4 (.in(1'b0), .out(transistor_3_out), .gate(E));
  Transistor transistor_5 (.in(Vdd), .out(transistor_5_out), .gate(transistor_1_out));
  Transistor transistor_6 (.in(Vdd), .out(transistor_6_out), .gate(B));
  Transistor #(.\type ("n")) transistor_7 (.in(1'b0), .out(transistor_6_out), .gate(B));
  Transistor transistor_8 (.in(Vdd), .out(transistor_8_out), .gate(transistor_3_out));
  Transistor transistor_9 (.in(Vdd), .out(transistor_9_out), .gate(F));
  Transistor #(.\type ("n")) transistor_10 (.in(1'b0), .out(transistor_9_out), .gate(F));
  Transistor transistor_11 (.in(Vdd), .out(transistor_5_out), .gate(transistor_6_out));
  Transistor transistor_12 (.in(Vdd), .out(J), .gate(transistor_5_out));
  Transistor #(.\type ("n")) transistor_13 (.in(1'b0), .out(J), .gate(transistor_5_out));
  Transistor #(.\type ("n")) transistor_14 (.in(transistor_15_out), .out(transistor_5_out), .gate(transistor_1_out));
  Transistor #(.\type ("n")) transistor_15 (.in(1'b0), .out(transistor_15_out), .gate(transistor_6_out));
  Transistor transistor_16 (.in(Vdd), .out(transistor_8_out), .gate(transistor_9_out));
  Transistor transistor_17 (.in(Vdd), .out(L), .gate(transistor_8_out));
  Transistor #(.\type ("n")) transistor_18 (.in(1'b0), .out(L), .gate(transistor_8_out));
  Transistor #(.\type ("n")) transistor_19 (.in(transistor_20_out), .out(transistor_8_out), .gate(transistor_3_out));
  Transistor #(.\type ("n")) transistor_20 (.in(1'b0), .out(transistor_20_out), .gate(transistor_9_out));
  Transistor transistor_21 (.in(Vdd), .out(transistor_21_out), .gate(transistor_22_out));
  Transistor transistor_22 (.in(Vdd), .out(transistor_22_out), .gate(D));
  Transistor #(.\type ("n")) transistor_23 (.in(1'b0), .out(transistor_22_out), .gate(D));
  Transistor transistor_24 (.in(Vdd), .out(transistor_24_out), .gate(C));
  Transistor #(.\type ("n")) transistor_25 (.in(1'b0), .out(transistor_24_out), .gate(C));
  Transistor transistor_26 (.in(Vdd), .out(transistor_26_out), .gate(transistor_27_out));
  Transistor transistor_27 (.in(Vdd), .out(transistor_27_out), .gate(H));
  Transistor #(.\type ("n")) transistor_28 (.in(1'b0), .out(transistor_27_out), .gate(H));
  Transistor transistor_29 (.in(Vdd), .out(transistor_29_out), .gate(G));
  Transistor #(.\type ("n")) transistor_30 (.in(1'b0), .out(transistor_29_out), .gate(G));
  Transistor transistor_31 (.in(Vdd), .out(transistor_21_out), .gate(transistor_24_out));
  Transistor #(.\type ("n")) transistor_32 (.in(transistor_33_out), .out(transistor_21_out), .gate(transistor_22_out));
  Transistor #(.\type ("n")) transistor_33 (.in(1'b0), .out(transistor_33_out), .gate(transistor_24_out));
  Transistor transistor_34 (.in(Vdd), .out(transistor_26_out), .gate(transistor_29_out));
  Transistor #(.\type ("n")) transistor_35 (.in(transistor_36_out), .out(transistor_26_out), .gate(transistor_27_out));
  Transistor #(.\type ("n")) transistor_36 (.in(1'b0), .out(transistor_36_out), .gate(transistor_29_out));
  Transistor transistor_37 (.in(Vdd), .out(K), .gate(transistor_21_out));
  Transistor #(.\type ("n")) transistor_38 (.in(1'b0), .out(K), .gate(transistor_21_out));
  Transistor transistor_39 (.in(Vdd), .out(M), .gate(transistor_26_out));
  Transistor #(.\type ("n")) transistor_40 (.in(1'b0), .out(M), .gate(transistor_26_out));
  // also tied to VCC on the sheet: Vdd
endmodule

module RCA_test (
  input  in_1,
  input  in_2,
  input  in_3,
  input  in_4,
  input  in_5,
  input  in_6,
  input  in_7,
  output out_8,
  output out_9,
  output out_10
);

  wire cd4000b_1_vss;

  CD4000B cd4000b_1 (
    .E(in_3), .D(in_5), .F(in_1), .C(in_6), .A(in_2), .B(in_4), .Vdd(1'b1), .G(in_7), .H(out_9), .K(out_8),
    .Vss(cd4000b_1_vss), .L(out_10));
  // also tied to GND on the sheet: cd4000b_1_vss
endmodule
